// Digital circuit cpu.dig as structural Verilog
module cpu (
  input  D0,
  input  D1,
  input  D2,
  input  D3,
  input  D4,
  input  D5,
  input  D6,
  input  D7,
  input  CLK,
  input  EN,
  input  E0,
  input  E1,
  input  E2,
  input  E3,
  input  E4,
  input  E5,
  input  E6,
  input  E7,
  input  MAN_OVERRIDE,
  input  MAN_D7,
  input  MAN_D6,
  input  MAN_D5,
  input  MAN_D4,
  input  MAN_D3,
  input  MAN_D2,
  input  MAN_D1,
  input  MAN_D0,
  input  MAN_A0,
  input  MAN_A1,
  input  MAN_A2,
  input  MAN_A3,
  input  MAN_CLK,
  input  MAN_CLK___HLT,
  input  MEMLOAD,
  input  MEMEI,
  input  MEMEO,
  input  MARO,
  input  MARCLR,
  input  MARLOAD,
  input  IREO,
  input  IRCLR,
  input  IRLOAD,
  input  PCEI,
  input  PCDEF,
  input  PCJ,
  input  PCEO,
  input  ALOAD,
  input  ACLR,
  input  AEO,
  input  ALUINVA,
  input  ALUEAI,
  input  ALUCI,
  input  ALUEBI,
  input  ALUINVB,
  input  BLOAD,
  input  BCLR,
  input  BEO,
  input  ALUEO,
  input  RST,
  input  EN_2,
  input  OLOAD,
  input  OCLR,
  input  OEO,
  input  MAN_LOAD,
  input  MASTER_RST,
  output CO
);

  wire and_1_out, and_2_out, and_3_out, and_4_out, and_5_out, and_6_out, and_7_out, and_8_out, and_9_out,
       and_10_out, and_11_out, and_12_out, and_13_out, and_14_out, and_15_out, and_16_out, and_17_out,
       and_18_out, and_19_out, and_20_out, and_21_out, and_22_out, and_23_out, and_24_out, and_25_out,
       and_26_out, and_27_out, and_28_out, and_29_out, and_30_out, and_31_out, and_32_out, and_33_out,
       and_34_out, and_35_out, and_36_out, and_37_out, and_38_out, and_39_out, and_40_out, and_41_out,
       and_42_out, and_43_out, and_44_out, and_45_out, and_46_out, and_47_out, and_48_out, and_49_out,
       and_50_out, and_51_out, and_52_out, and_53_out, and_54_out, and_55_out, and_56_out, and_57_out,
       and_58_out, and_59_out, and_60_out, and_61_out, and_62_out, and_63_out, and_64_out, and_65_out,
       and_66_out, and_67_out, and_68_out, and_69_out, and_70_out, and_71_out, and_72_out, and_73_out,
       and_74_out, and_75_out, and_76_out, and_77_out, and_78_out, and_79_out, and_80_out, and_81_out,
       and_82_out, and_83_out, and_84_out, and_85_out, and_86_out, and_87_out, and_88_out, and_89_out,
       and_90_out, and_91_out, and_92_out, and_93_out, and_94_out, and_95_out, and_96_out, and_97_out,
       and_98_out, and_99_out, and_100_out, and_101_out, and_102_out, and_103_out, and_104_out, and_105_out,
       and_106_out, and_107_out, and_108_out, and_109_out, and_110_out, and_111_out, and_112_out,
       and_113_out, and_114_out, and_115_out, and_116_out, and_117_out, and_118_out, and_119_out,
       and_120_out, and_121_out, and_122_out, and_123_out, and_124_out, and_125_out, and_126_out,
       and_127_out, and_128_out, and_129_out, and_130_out, and_131_out, and_132_out, and_133_out,
       and_134_out, and_135_out, and_136_out, and_137_out, and_138_out, and_139_out, and_140_out,
       and_141_out, and_142_out, and_143_out, and_144_out, and_145_out, and_146_out, and_147_out,
       and_148_out, and_149_out, and_150_out, and_151_out, and_152_out, and_153_out, and_154_out,
       and_155_out, and_156_out, and_157_out, and_158_out, and_159_out, and_160_out, and_161_out,
       and_162_out, and_163_out, and_164_out, and_165_out, and_166_out, and_167_out, and_168_out,
       and_169_out, and_170_out, and_171_out, and_172_out, and_173_out, and_174_out, and_175_out,
       and_176_out, and_177_out, and_178_out, and_179_out, and_180_out, and_181_out, and_182_out,
       and_183_out, and_184_out, and_185_out, and_186_out, and_187_out, and_188_out, and_189_out,
       and_190_out, and_191_out, and_192_out, and_193_out, and_194_out, and_195_out, and_196_out,
       and_197_out, and_198_out, and_199_out, and_200_out, and_201_out, and_202_out, and_203_out,
       and_204_out, and_205_out, and_206_out, and_207_out, and_208_out, and_209_out, and_210_out,
       and_211_out, and_212_out, and_213_out, and_214_out, and_215_out, and_216_out, and_217_out,
       and_218_out, and_219_out, and_220_out, and_221_out, and_222_out, and_223_out, and_224_out,
       and_225_out, and_226_out, and_227_out, and_228_out, and_229_out, and_230_out, and_231_out,
       and_232_out, and_233_out, and_234_out, and_235_out, and_236_out, and_237_out, and_238_out,
       and_239_out, and_240_out, and_241_out, and_242_out, and_243_out, and_244_out, and_245_out,
       and_246_out, and_247_out, and_248_out, and_249_out, and_250_out, and_251_out, and_252_out,
       and_253_out, and_254_out, and_255_out, and_256_out, and_257_out, and_258_out, and_259_out,
       and_260_out, and_261_out, and_262_out, and_263_out, and_264_out, and_265_out, and_266_out,
       and_267_out, and_268_out, and_269_out, and_270_out, and_271_out, and_272_out, and_273_out,
       and_274_out, and_275_out, and_276_out, and_277_out, and_278_out, and_279_out, and_280_out,
       and_281_out, and_282_out, and_283_out, and_284_out, and_285_out, and_286_out, and_287_out,
       and_288_out, and_289_out, and_290_out, and_291_out, and_292_out, and_293_out, and_294_out,
       and_295_out, and_296_out, and_297_out, and_298_out, and_299_out, and_300_out, and_301_out,
       and_302_out, and_303_out, and_304_out, and_305_out, and_306_out, and_307_out, and_308_out,
       and_309_out, and_310_out, and_311_out, and_312_out, and_313_out, and_314_out, and_315_out,
       and_316_out, and_317_out, and_318_out, and_319_out, and_320_out, and_321_out, and_322_out,
       and_323_out, and_324_out, and_325_out, and_326_out, and_327_out, and_328_out, and_329_out,
       and_330_out, and_331_out, and_332_out, and_333_out, and_334_out, and_335_out, and_336_out,
       and_337_out, and_338_out, and_339_out, and_340_out, and_341_out, and_342_out, and_343_out,
       and_344_out, and_345_out, and_346_out, and_347_out, and_348_out, and_349_out, and_350_out,
       and_351_out, and_352_out, and_353_out, and_354_out, and_355_out, and_356_out, and_357_out,
       and_358_out, and_359_out, and_360_out, and_361_out, and_362_out, and_363_out, and_364_out,
       and_365_out, and_366_out, and_367_out, and_368_out, and_369_out, and_370_out, and_371_out,
       and_372_out, and_373_out, and_374_out, and_375_out, and_376_out, and_377_out, and_378_out,
       and_379_out, and_380_out, and_381_out, and_382_out, and_383_out, and_384_out, and_385_out,
       and_386_out, and_387_out, and_388_out, and_389_out, and_390_out, and_391_out, and_392_out,
       and_393_out, and_394_out, and_395_out, and_396_out, and_397_out, and_398_out, and_399_out,
       and_400_out, and_401_out, and_402_out, and_403_out, and_404_out, and_405_out, and_406_out,
       and_407_out, and_408_out, and_409_out, and_410_out, and_411_out, and_412_out, and_413_out,
       and_414_out, and_415_out, and_416_out, and_417_out, and_418_out, and_419_out, and_420_out,
       and_421_out, and_422_out, and_423_out, and_424_out, and_425_out, and_426_out, and_427_out,
       and_428_out, and_429_out, and_430_out, and_431_out, and_432_out, and_433_out, and_434_out,
       and_435_out, and_436_out, and_437_out, and_438_out, and_439_out, and_440_out, and_441_out,
       and_442_out, and_443_out, and_444_out, and_445_out, and_446_out, and_447_out, and_448_out,
       and_449_out, and_450_out, and_451_out, and_452_out, and_453_out, and_454_out, and_455_out,
       and_456_out, and_457_out, and_458_out, and_459_out, and_460_out, and_461_out, and_462_out,
       and_463_out, and_464_out, and_465_out, and_466_out, and_467_out, and_468_out, and_469_out,
       and_470_out, and_471_out, and_472_out, and_473_out, and_474_out, and_475_out, and_476_out,
       and_477_out, and_478_out, and_479_out, and_480_out, and_481_out, and_482_out, and_483_out,
       and_484_out, and_485_out, and_486_out, and_487_out, and_488_out, and_489_out, and_490_out,
       and_491_out, and_492_out, and_493_out, and_494_out, and_495_out, and_496_out, and_497_out,
       and_498_out, and_499_out, and_500_out, and_501_out, and_502_out, and_503_out, and_504_out,
       and_505_out, and_506_out, and_507_out, and_508_out, and_509_out, and_510_out, and_511_out,
       and_512_out, and_513_out, and_514_out, and_515_out, and_516_out, and_517_out, and_518_out,
       and_519_out, and_520_out, and_521_out, and_522_out, and_523_out, and_524_out, and_525_out,
       and_526_out, and_527_out, and_528_out, and_529_out, and_530_out, and_531_out, and_532_out,
       and_533_out, and_534_out, and_535_out, and_536_out, and_537_out, and_538_out, and_539_out,
       and_540_out, and_541_out, and_542_out, and_543_out, and_544_out, and_545_out, and_546_out,
       and_547_out, and_548_out, and_549_out, and_550_out, and_551_out, and_552_out, and_553_out,
       and_554_out, and_555_out, and_556_out, and_557_out, and_558_out, and_559_out, and_560_out,
       and_561_out, and_562_out, and_563_out, and_564_out, and_565_out, and_566_out, and_567_out,
       and_568_out, and_569_out, and_570_out, and_571_out, and_572_out, and_573_out, and_574_out,
       and_575_out, and_576_out, and_577_out, and_578_out, and_579_out, and_580_out, and_581_out,
       and_582_out, and_583_out, and_584_out, and_585_out, and_586_out, and_587_out, and_588_out,
       and_589_out, and_590_out, and_591_out, and_592_out, and_593_out, and_594_out, and_595_out,
       and_596_out, and_597_out, and_598_out, and_599_out, and_600_out, and_601_out, and_602_out,
       and_603_out, and_604_out, and_605_out, and_606_out, and_607_out, and_608_out, and_609_out,
       and_610_out, and_611_out, and_612_out, and_613_out, and_614_out, and_615_out, and_616_out,
       and_617_out, and_618_out, and_619_out, and_620_out, and_621_out, and_622_out, and_623_out,
       and_624_out, and_625_out, and_626_out, and_627_out, and_628_out, and_629_out, and_630_out,
       and_631_out, and_632_out, and_633_out, and_634_out, and_635_out, and_636_out, and_637_out,
       and_638_out, and_639_out, and_640_out, and_641_out, and_642_out, and_643_out, and_644_out,
       and_645_out, and_646_out, and_647_out, and_648_out, and_649_out, and_650_out, and_651_out,
       and_652_out, and_653_out, and_654_out, and_655_out, and_656_out, and_657_out, and_658_out,
       and_659_out, and_660_out, and_661_out, and_662_out, and_663_out, and_664_out, and_665_out,
       and_666_out, and_667_out, and_668_out, and_669_out, and_670_out, and_671_out, and_672_out,
       and_673_out, and_674_out, and_675_out, and_676_out, and_677_out, and_678_out, and_679_out,
       and_680_out, and_681_out, and_682_out, and_683_out, and_684_out, and_685_out, and_686_out,
       and_687_out, and_688_out, and_689_out, and_690_out, and_691_out, and_692_out, driver_27_out,
       driver_38_out, driver_54_out, driver_70_out, driver_86_out, driver_102_out, driver_122_out,
       driver_146_out, driver_162_out, driver_229_out, driver_234_out, driver_237_out, driver_240_out,
       driver_241_out, driver_254_out, driver_259_out, driver_263_out, driver_268_out, driver_271_out,
       driver_274_out, driver_275_out, driver_288_out, driver_293_out, MAN_EI_out, nor_1_out, nor_2_out,
       nor_3_out, nor_4_out, nor_5_out, nor_6_out, nor_7_out, nor_8_out, nor_9_out, nor_10_out, nor_11_out,
       nor_12_out, nor_13_out, nor_14_out, nor_15_out, nor_16_out, nor_17_out, nor_18_out, nor_19_out,
       nor_20_out, nor_21_out, nor_22_out, nor_23_out, nor_24_out, nor_25_out, nor_26_out, nor_27_out,
       nor_28_out, nor_29_out, nor_30_out, nor_31_out, nor_32_out, nor_33_out, nor_34_out, nor_35_out,
       nor_36_out, nor_37_out, nor_38_out, nor_39_out, nor_40_out, nor_41_out, nor_42_out, nor_43_out,
       nor_44_out, nor_45_out, nor_46_out, nor_47_out, nor_48_out, nor_49_out, nor_50_out, nor_51_out,
       nor_52_out, nor_53_out, nor_54_out, nor_55_out, nor_56_out, nor_57_out, nor_58_out, nor_59_out,
       nor_60_out, nor_61_out, nor_62_out, nor_63_out, nor_64_out, nor_65_out, nor_66_out, nor_67_out,
       nor_68_out, nor_69_out, nor_70_out, nor_71_out, nor_72_out, nor_73_out, nor_74_out, nor_75_out,
       nor_76_out, nor_77_out, nor_78_out, nor_79_out, nor_80_out, nor_81_out, nor_82_out, nor_83_out,
       nor_84_out, nor_85_out, nor_86_out, nor_87_out, nor_88_out, nor_89_out, nor_90_out, nor_91_out,
       nor_92_out, nor_93_out, nor_94_out, nor_95_out, nor_96_out, nor_97_out, nor_98_out, nor_99_out,
       nor_100_out, nor_101_out, nor_102_out, nor_103_out, nor_104_out, nor_105_out, nor_106_out,
       nor_107_out, nor_108_out, nor_109_out, nor_110_out, nor_111_out, nor_112_out, nor_113_out,
       nor_114_out, nor_115_out, nor_116_out, nor_117_out, nor_118_out, nor_119_out, nor_120_out,
       nor_121_out, nor_122_out, nor_123_out, nor_124_out, nor_125_out, nor_126_out, nor_127_out,
       nor_128_out, nor_129_out, nor_130_out, nor_131_out, nor_132_out, nor_133_out, nor_134_out,
       nor_135_out, nor_136_out, nor_137_out, nor_138_out, nor_139_out, nor_140_out, nor_141_out,
       nor_142_out, nor_143_out, nor_144_out, nor_145_out, nor_146_out, nor_147_out, nor_148_out,
       nor_149_out, nor_150_out, nor_151_out, nor_152_out, nor_153_out, nor_154_out, nor_155_out,
       nor_156_out, nor_157_out, nor_158_out, nor_159_out, nor_160_out, nor_161_out, nor_162_out,
       nor_163_out, nor_164_out, nor_165_out, nor_166_out, nor_167_out, nor_168_out, nor_169_out,
       nor_170_out, nor_171_out, nor_172_out, nor_173_out, nor_174_out, nor_175_out, nor_176_out,
       nor_177_out, nor_178_out, nor_179_out, nor_180_out, nor_181_out, nor_182_out, nor_183_out,
       nor_184_out, nor_185_out, nor_186_out, nor_187_out, nor_188_out, nor_189_out, nor_190_out,
       nor_191_out, nor_192_out, nor_193_out, nor_194_out, nor_195_out, nor_196_out, nor_197_out,
       nor_198_out, nor_199_out, nor_200_out, nor_201_out, nor_202_out, nor_203_out, nor_204_out,
       nor_205_out, nor_206_out, nor_207_out, nor_208_out, nor_209_out, nor_210_out, nor_211_out,
       nor_212_out, nor_213_out, nor_214_out, nor_215_out, nor_216_out, nor_217_out, nor_218_out,
       nor_219_out, nor_220_out, nor_221_out, nor_222_out, nor_223_out, nor_224_out, nor_225_out,
       nor_226_out, nor_227_out, nor_228_out, nor_229_out, nor_230_out, nor_231_out, nor_232_out,
       nor_233_out, nor_234_out, nor_235_out, nor_236_out, nor_237_out, nor_238_out, nor_239_out,
       nor_240_out, nor_241_out, nor_242_out, nor_243_out, nor_244_out, nor_245_out, nor_246_out,
       nor_247_out, nor_248_out, nor_249_out, nor_250_out, nor_251_out, nor_252_out, nor_253_out,
       nor_254_out, nor_255_out, nor_256_out, nor_257_out, nor_258_out, nor_259_out, nor_260_out,
       nor_261_out, nor_262_out, nor_263_out, nor_264_out, nor_265_out, nor_266_out, nor_267_out,
       nor_268_out, nor_269_out, nor_270_out, nor_271_out, nor_272_out, nor_273_out, nor_274_out,
       nor_275_out, nor_276_out, nor_277_out, nor_278_out, nor_279_out, nor_280_out, nor_281_out,
       nor_282_out, nor_283_out, nor_284_out, nor_285_out, nor_286_out, nor_287_out, nor_288_out,
       nor_289_out, nor_290_out, nor_291_out, nor_292_out, nor_293_out, nor_294_out, nor_295_out,
       nor_296_out, nor_297_out, nor_298_out, nor_299_out, nor_300_out, nor_301_out, nor_302_out,
       nor_303_out, nor_304_out, nor_305_out, nor_306_out, nor_307_out, nor_308_out, nor_309_out,
       nor_310_out, nor_311_out, nor_312_out, nor_313_out, nor_314_out, nor_315_out, nor_316_out,
       nor_317_out, nor_318_out, nor_319_out, nor_320_out, nor_321_out, nor_322_out, nor_323_out,
       nor_324_out, nor_325_out, nor_326_out, nor_327_out, nor_328_out, nor_329_out, nor_330_out,
       nor_331_out, nor_332_out, nor_333_out, nor_334_out, nor_335_out, nor_336_out, nor_337_out,
       nor_338_out, nor_339_out, nor_340_out, nor_341_out, nor_342_out, nor_343_out, nor_344_out,
       nor_345_out, nor_346_out, nor_347_out, nor_348_out, nor_349_out, nor_350_out, nor_351_out,
       nor_352_out, not_1_out, not_2_out, not_3_out, not_4_out, not_5_out, not_6_out, not_7_out, not_8_out,
       not_9_out, not_10_out, not_11_out, not_12_out, not_13_out, not_14_out, not_15_out, not_16_out,
       not_17_out, not_18_out, not_19_out, not_20_out, not_21_out, not_22_out, not_23_out, not_24_out,
       not_25_out, not_26_out, not_27_out, not_28_out, not_29_out, not_30_out, not_31_out, not_32_out,
       not_33_out, not_34_out, not_35_out, not_36_out, not_37_out, not_38_out, not_39_out, not_40_out,
       not_41_out, not_42_out, not_43_out, not_44_out, not_45_out, not_46_out, not_47_out, not_48_out,
       not_49_out, not_50_out, not_51_out, not_52_out, not_53_out, not_54_out, not_55_out, not_56_out,
       or_1_out, or_2_out, or_3_out, or_4_out, or_5_out, or_6_out, or_7_out, or_8_out, or_9_out, or_10_out,
       or_11_out, or_12_out, or_13_out, or_14_out, or_15_out, or_16_out, or_17_out, or_18_out, or_19_out,
       or_20_out, or_21_out, or_22_out, or_23_out, or_24_out, or_25_out, or_26_out, or_27_out, or_28_out,
       or_29_out, or_30_out, or_31_out, or_32_out, or_33_out, or_34_out, or_35_out, or_36_out, or_37_out,
       or_38_out, or_39_out, or_40_out, or_41_out, or_42_out, or_43_out, or_44_out, or_45_out, or_46_out,
       or_47_out, or_48_out, or_49_out, or_50_out, or_51_out, or_52_out, or_53_out, or_54_out, or_55_out,
       or_56_out, or_57_out, or_58_out, or_59_out, or_60_out, or_61_out, or_62_out, or_63_out, or_64_out,
       or_65_out, or_66_out, or_67_out, or_68_out, or_69_out, or_70_out, or_71_out, or_72_out, or_73_out,
       or_74_out, or_75_out, or_76_out, or_77_out, or_78_out, or_79_out, or_80_out, or_81_out, or_82_out,
       or_83_out, or_84_out, or_85_out, or_87_out, or_88_out, or_89_out, or_90_out, or_91_out, or_92_out,
       or_93_out, or_94_out, or_95_out, or_96_out, or_97_out, or_98_out, or_99_out, or_100_out, or_101_out,
       or_102_out, or_103_out, or_104_out, or_105_out, or_106_out, or_107_out, or_108_out, or_109_out,
       xor_1_out, xor_2_out, xor_3_out, xor_4_out, xor_5_out, xor_6_out, xor_7_out, xor_8_out, xor_9_out,
       xor_10_out, xor_11_out, xor_12_out, xor_13_out, xor_14_out, xor_15_out, xor_16_out, xor_17_out,
       xor_18_out, xor_19_out, xor_20_out, xor_21_out, xor_22_out, xor_23_out, xor_24_out, xor_25_out,
       xor_26_out, xor_27_out, xor_28_out, xor_29_out, xor_30_out, xor_31_out, xor_32_out, xor_33_out,
       xor_34_out, xor_35_out, xor_36_out;

  and and_1 (and_1_out, MAN_OVERRIDE, MAN_A0);
  and and_2 (and_2_out, nor_169_out, ~MAN_OVERRIDE);  // And
  or or_1 (or_1_out, and_2_out, and_1_out);
  and and_3 (and_3_out, MAN_OVERRIDE, MAN_A1);
  or or_2 (or_2_out, and_6_out, and_3_out);
  and and_4 (and_4_out, ~nor_39_out, and_172_out);  // And
  and and_5 (and_5_out, and_172_out, nor_39_out);
  not not_1 (not_1_out, MASTER_RST);
  and and_6 (and_6_out, nor_171_out, ~MAN_OVERRIDE);  // And
  or or_3 (or_3_out, and_5_out, MASTER_RST);
  assign MEMLOAD = and_256_out ? and_256_out : 1'bz;  // Driver driver_1
  assign MEMLOAD = and_255_out ? and_255_out : 1'bz;  // Driver driver_2
  and and_7 (and_7_out, MAN_OVERRIDE, MAN_A2);
  or or_4 (or_4_out, and_8_out, and_7_out);
  nor nor_1 (nor_1_out, and_4_out, nor_2_out);
  nor nor_2 (nor_2_out, nor_1_out, or_3_out);
  assign MEMEI = and_256_out ? and_256_out : 1'bz;  // Driver driver_3
  and and_8 (and_8_out, nor_173_out, ~MAN_OVERRIDE);  // And
  assign MEMEI = and_255_out ? and_255_out : 1'bz;  // Driver driver_4
  and and_9 (and_9_out, MAN_OVERRIDE, MAN_A3);
  and and_10 (and_10_out, nor_1_out, not_1_out);
  not not_2 (not_2_out, MAN_OVERRIDE);
  and and_11 (and_11_out, nor_175_out, ~MAN_OVERRIDE);  // And
  or or_5 (or_5_out, and_11_out, and_9_out);
  and and_12 (and_12_out, ~nor_1_out, and_172_out);  // And
  and and_13 (and_13_out, and_172_out, nor_1_out);
  not not_3 (not_3_out, nor_217_out);
  not not_4 (not_4_out, nor_219_out);
  assign MEMEO = and_56_out ? and_56_out : 1'bz;  // Driver driver_5
  assign MARLOAD = and_10_out ? and_10_out : 1'bz;  // Driver driver_6
  or or_6 (or_6_out, MASTER_RST, and_12_out);
  nor nor_3 (nor_3_out, or_6_out, nor_4_out);
  nor nor_4 (nor_4_out, nor_3_out, and_13_out);
  not not_5 (not_5_out, nor_221_out);
  not not_6 (not_6_out, nor_223_out);
  assign IRLOAD = and_56_out ? and_56_out : 1'bz;  // Driver driver_7
  assign PCDEF = and_56_out ? and_56_out : 1'bz;  // Driver driver_8
  and and_14 (and_14_out, MAN_OVERRIDE, MAN_D0);
  and and_15 (and_15_out, not_3_out, not_4_out);
  and and_16 (and_16_out, not_5_out, nor_223_out);
  and and_17 (and_17_out, nor_221_out, not_6_out);
  and and_18 (and_18_out, nor_217_out, nor_219_out);
  and and_19 (and_19_out, nor_221_out, nor_223_out);
  and and_20 (and_20_out, not_3_out, nor_219_out);
  and and_21 (and_21_out, not_6_out, not_5_out);
  and and_22 (and_22_out, not_4_out, nor_217_out);
  assign PCEO = and_10_out ? and_10_out : 1'bz;  // Driver driver_9
  assign ALOAD = and_219_out ? and_219_out : 1'bz;  // Driver driver_10
  and and_23 (and_23_out, driver_38_out, not_2_out);
  or or_7 (or_7_out, and_23_out, and_14_out);
  and and_24 (and_24_out, ~or_1_out, ~or_2_out);  // And
  and and_25 (and_25_out, ~or_4_out, ~or_5_out);  // And
  and and_26 (and_26_out, or_1_out, ~or_2_out);  // And
  and and_27 (and_27_out, ~or_4_out, ~or_5_out);  // And
  and and_28 (and_28_out, ~or_1_out, or_2_out);  // And
  and and_29 (and_29_out, ~or_4_out, ~or_5_out);  // And
  and and_30 (and_30_out, or_1_out, or_2_out);
  and and_31 (and_31_out, ~or_4_out, ~or_5_out);  // And
  and and_32 (and_32_out, ~or_1_out, ~or_2_out);  // And
  and and_33 (and_33_out, or_4_out, ~or_5_out);  // And
  and and_34 (and_34_out, or_1_out, ~or_2_out);  // And
  and and_35 (and_35_out, or_4_out, ~or_5_out);  // And
  and and_36 (and_36_out, ~or_1_out, or_2_out);  // And
  and and_37 (and_37_out, or_4_out, ~or_5_out);  // And
  and and_38 (and_38_out, or_1_out, or_2_out);
  and and_39 (and_39_out, or_4_out, ~or_5_out);  // And
  and and_40 (and_40_out, ~or_1_out, ~or_2_out);  // And
  and and_41 (and_41_out, ~or_4_out, or_5_out);  // And
  and and_42 (and_42_out, or_1_out, ~or_2_out);  // And
  and and_43 (and_43_out, ~or_4_out, or_5_out);  // And
  and and_44 (and_44_out, ~or_1_out, or_2_out);  // And
  and and_45 (and_45_out, ~or_4_out, or_5_out);  // And
  and and_46 (and_46_out, or_1_out, or_2_out);
  and and_47 (and_47_out, ~or_4_out, or_5_out);  // And
  and and_48 (and_48_out, ~or_1_out, ~or_2_out);  // And
  and and_49 (and_49_out, or_4_out, or_5_out);
  and and_50 (and_50_out, or_1_out, ~or_2_out);  // And
  and and_51 (and_51_out, or_4_out, or_5_out);
  and and_52 (and_52_out, ~or_1_out, or_2_out);  // And
  and and_53 (and_53_out, or_4_out, or_5_out);
  and and_54 (and_54_out, or_1_out, or_2_out);
  and and_55 (and_55_out, or_4_out, or_5_out);
  and and_56 (and_56_out, nor_3_out, not_1_out);
  assign IREO = or_11_out ? or_11_out : 1'bz;  // Driver driver_11
  assign MARLOAD = or_11_out ? or_11_out : 1'bz;  // Driver driver_12
  assign MEMEO = and_219_out ? and_219_out : 1'bz;  // Driver driver_13
  assign AEO = and_93_out ? and_93_out : 1'bz;  // Driver driver_14
  and and_57 (and_57_out, MAN_OVERRIDE, MAN_D1);
  and and_58 (and_58_out, and_97_out, ~MAN_OVERRIDE);  // And
  and and_59 (and_59_out, MAN_OVERRIDE, MAN_LOAD);
  and and_60 (and_60_out, and_80_out, and_131_out);
  assign MEMEO = and_254_out ? and_254_out : 1'bz;  // Driver driver_15
  assign BLOAD = and_254_out ? and_254_out : 1'bz;  // Driver driver_16
  and and_61 (and_61_out, driver_54_out, not_2_out);
  or or_8 (or_8_out, and_61_out, and_57_out);
  DipSwitch #(.dipDefault("true")) MAN_EI (.out(MAN_EI_out));
  or or_9 (or_9_out, and_58_out, and_59_out);
  and and_62 (and_62_out, and_24_out, and_25_out);
  and and_63 (and_63_out, and_26_out, and_27_out);
  and and_64 (and_64_out, and_28_out, and_29_out);
  and and_65 (and_65_out, and_30_out, and_31_out);
  and and_66 (and_66_out, and_32_out, and_33_out);
  and and_67 (and_67_out, and_34_out, and_35_out);
  and and_68 (and_68_out, and_36_out, and_37_out);
  and and_69 (and_69_out, and_38_out, and_39_out);
  and and_70 (and_70_out, and_40_out, and_41_out);
  and and_71 (and_71_out, and_42_out, and_43_out);
  and and_72 (and_72_out, and_44_out, and_45_out);
  and and_73 (and_73_out, and_46_out, and_47_out);
  and and_74 (and_74_out, and_48_out, and_49_out);
  and and_75 (and_75_out, and_50_out, and_51_out);
  and and_76 (and_76_out, and_52_out, and_53_out);
  and and_77 (and_77_out, and_54_out, and_55_out);
  and and_78 (and_78_out, ~nor_3_out, and_172_out);  // And
  and and_79 (and_79_out, and_172_out, nor_3_out);
  and and_80 (and_80_out, and_15_out, and_16_out);
  and and_81 (and_81_out, and_15_out, and_17_out);
  and and_82 (and_82_out, and_18_out, and_17_out);
  and and_83 (and_83_out, and_18_out, and_19_out);
  and and_84 (and_84_out, and_15_out, and_19_out);
  and and_85 (and_85_out, and_20_out, and_21_out);
  and and_86 (and_86_out, and_20_out, and_16_out);
  and and_87 (and_87_out, and_20_out, and_17_out);
  and and_88 (and_88_out, and_20_out, and_19_out);
  and and_89 (and_89_out, and_22_out, and_21_out);
  and and_90 (and_90_out, and_22_out, and_16_out);
  and and_91 (and_91_out, and_81_out, and_131_out);
  or or_10 (or_10_out, and_91_out, and_60_out);
  or or_11 (or_11_out, or_18_out, or_10_out);
  assign PCEI = and_215_out ? and_215_out : 1'bz;  // Driver driver_17
  assign PCJ = and_215_out ? and_215_out : 1'bz;  // Driver driver_18
  assign IREO = and_215_out ? and_215_out : 1'bz;  // Driver driver_19
  assign BLOAD = and_180_out ? and_180_out : 1'bz;  // Driver driver_20
  assign IREO = and_180_out ? and_180_out : 1'bz;  // Driver driver_21
  assign ALOAD = and_177_out ? and_177_out : 1'bz;  // Driver driver_22
  assign IREO = and_177_out ? and_177_out : 1'bz;  // Driver driver_23
  assign OLOAD = and_93_out ? and_93_out : 1'bz;  // Driver driver_24
  and and_92 (and_92_out, MAN_OVERRIDE, MAN_D2);
  or or_12 (or_12_out, MASTER_RST, and_78_out);
  nor nor_5 (nor_5_out, or_12_out, nor_6_out);
  nor nor_6 (nor_6_out, nor_5_out, and_79_out);
  and and_93 (and_93_out, and_82_out, and_131_out);
  assign BEO = and_256_out ? and_256_out : 1'bz;  // Driver driver_25
  assign AEO = and_255_out ? and_255_out : 1'bz;  // Driver driver_26
  assign driver_27_out = and_95_out ? and_95_out : 1'bz;  // Driver driver_27
  and and_94 (and_94_out, driver_70_out, not_2_out);
  or or_13 (or_13_out, and_94_out, and_92_out);
  not not_7 (not_7_out, or_9_out);
  not not_8 (not_8_out, not_7_out);
  and and_95 (and_95_out, and_83_out, and_131_out);
  and and_96 (and_96_out, MAN_OVERRIDE, MAN_D3);
  and and_97 (and_97_out, or_46_out, MEMLOAD);
  and and_98 (and_98_out, or_9_out, ~not_8_out);  // And
  and and_99 (and_99_out, and_62_out, MEMEO);
  and and_100 (and_100_out, and_62_out, and_98_out);
  and and_101 (and_101_out, and_63_out, MEMEO);
  and and_102 (and_102_out, and_63_out, and_98_out);
  and and_103 (and_103_out, and_64_out, MEMEO);
  and and_104 (and_104_out, and_64_out, and_98_out);
  and and_105 (and_105_out, and_65_out, MEMEO);
  and and_106 (and_106_out, and_65_out, and_98_out);
  and and_107 (and_107_out, and_66_out, MEMEO);
  and and_108 (and_108_out, and_66_out, and_98_out);
  and and_109 (and_109_out, and_67_out, MEMEO);
  and and_110 (and_110_out, and_67_out, and_98_out);
  and and_111 (and_111_out, and_68_out, MEMEO);
  and and_112 (and_112_out, and_68_out, and_98_out);
  and and_113 (and_113_out, and_69_out, MEMEO);
  and and_114 (and_114_out, and_69_out, and_98_out);
  and and_115 (and_115_out, and_70_out, MEMEO);
  and and_116 (and_116_out, and_70_out, and_98_out);
  and and_117 (and_117_out, and_71_out, MEMEO);
  and and_118 (and_118_out, and_71_out, and_98_out);
  and and_119 (and_119_out, and_72_out, MEMEO);
  and and_120 (and_120_out, and_72_out, and_98_out);
  and and_121 (and_121_out, and_73_out, MEMEO);
  and and_122 (and_122_out, and_73_out, and_98_out);
  and and_123 (and_123_out, and_74_out, MEMEO);
  and and_124 (and_124_out, and_74_out, and_98_out);
  and and_125 (and_125_out, and_75_out, MEMEO);
  and and_126 (and_126_out, and_75_out, and_98_out);
  and and_127 (and_127_out, and_76_out, MEMEO);
  and and_128 (and_128_out, and_76_out, and_98_out);
  and and_129 (and_129_out, and_77_out, MEMEO);
  and and_130 (and_130_out, and_77_out, and_98_out);
  and and_131 (and_131_out, nor_5_out, not_1_out);
  and and_132 (and_132_out, and_84_out, and_131_out);
  and and_133 (and_133_out, driver_86_out, not_2_out);
  or or_14 (or_14_out, and_133_out, and_96_out);
  and and_134 (and_134_out, MAN_OVERRIDE, MAN_EI_out);
  or or_15 (or_15_out, and_136_out, and_134_out);
  and and_135 (and_135_out, and_85_out, and_131_out);
  and and_136 (and_136_out, MEMEI, ~MAN_OVERRIDE);  // And
  and and_137 (and_137_out, or_7_out, or_15_out);
  and and_138 (and_138_out, ~and_137_out, and_100_out);  // And
  and and_139 (and_139_out, and_100_out, and_137_out);
  and and_140 (and_140_out, ~and_137_out, and_102_out);  // And
  and and_141 (and_141_out, and_102_out, and_137_out);
  and and_142 (and_142_out, ~and_137_out, and_104_out);  // And
  and and_143 (and_143_out, and_104_out, and_137_out);
  and and_144 (and_144_out, ~and_137_out, and_106_out);  // And
  and and_145 (and_145_out, and_106_out, and_137_out);
  and and_146 (and_146_out, ~and_137_out, and_108_out);  // And
  and and_147 (and_147_out, and_108_out, and_137_out);
  and and_148 (and_148_out, ~and_137_out, and_110_out);  // And
  and and_149 (and_149_out, and_110_out, and_137_out);
  and and_150 (and_150_out, ~and_137_out, and_112_out);  // And
  and and_151 (and_151_out, and_112_out, and_137_out);
  and and_152 (and_152_out, ~and_137_out, and_114_out);  // And
  and and_153 (and_153_out, and_114_out, and_137_out);
  and and_154 (and_154_out, ~and_137_out, and_116_out);  // And
  and and_155 (and_155_out, and_116_out, and_137_out);
  and and_156 (and_156_out, ~and_137_out, and_118_out);  // And
  and and_157 (and_157_out, and_118_out, and_137_out);
  and and_158 (and_158_out, ~and_137_out, and_120_out);  // And
  and and_159 (and_159_out, and_120_out, and_137_out);
  and and_160 (and_160_out, ~and_137_out, and_122_out);  // And
  and and_161 (and_161_out, and_122_out, and_137_out);
  and and_162 (and_162_out, ~and_137_out, and_124_out);  // And
  and and_163 (and_163_out, and_124_out, and_137_out);
  and and_164 (and_164_out, ~and_137_out, and_126_out);  // And
  and and_165 (and_165_out, and_126_out, and_137_out);
  and and_166 (and_166_out, ~and_137_out, and_128_out);  // And
  and and_167 (and_167_out, and_128_out, and_137_out);
  and and_168 (and_168_out, ~and_137_out, and_130_out);  // And
  and and_169 (and_169_out, and_130_out, and_137_out);
  and and_170 (and_170_out, ~nor_5_out, and_172_out);  // And
  and and_171 (and_171_out, and_172_out, nor_5_out);
  and and_172 (and_172_out, ~not_9_out, not_11_out);  // And
  not not_9 (not_9_out, not_10_out);
  not not_10 (not_10_out, not_11_out);
  and and_173 (and_173_out, and_86_out, and_131_out);
  assign ALUEO = and_132_out ? and_132_out : 1'bz;  // Driver driver_28
  assign ALUEBI = and_132_out ? and_132_out : 1'bz;  // Driver driver_29
  assign ALUEAI = and_132_out ? and_132_out : 1'bz;  // Driver driver_30
  assign ALOAD = and_132_out ? and_132_out : 1'bz;  // Driver driver_31
  and and_174 (and_174_out, MAN_OVERRIDE, MAN_D4);
  or or_16 (or_16_out, and_176_out, and_174_out);
  nor nor_7 (nor_7_out, and_138_out, nor_8_out);
  nor nor_8 (nor_8_out, nor_7_out, and_139_out);
  nor nor_9 (nor_9_out, and_140_out, nor_10_out);
  nor nor_10 (nor_10_out, nor_9_out, and_141_out);
  nor nor_11 (nor_11_out, and_142_out, nor_12_out);
  nor nor_12 (nor_12_out, nor_11_out, and_143_out);
  nor nor_13 (nor_13_out, and_144_out, nor_14_out);
  nor nor_14 (nor_14_out, nor_13_out, and_145_out);
  nor nor_15 (nor_15_out, and_146_out, nor_16_out);
  nor nor_16 (nor_16_out, nor_15_out, and_147_out);
  nor nor_17 (nor_17_out, and_148_out, nor_18_out);
  nor nor_18 (nor_18_out, nor_17_out, and_149_out);
  nor nor_19 (nor_19_out, and_150_out, nor_20_out);
  nor nor_20 (nor_20_out, nor_19_out, and_151_out);
  nor nor_21 (nor_21_out, and_152_out, nor_22_out);
  nor nor_22 (nor_22_out, nor_21_out, and_153_out);
  nor nor_23 (nor_23_out, and_154_out, nor_24_out);
  nor nor_24 (nor_24_out, nor_23_out, and_155_out);
  nor nor_25 (nor_25_out, and_156_out, nor_26_out);
  nor nor_26 (nor_26_out, nor_25_out, and_157_out);
  nor nor_27 (nor_27_out, and_158_out, nor_28_out);
  nor nor_28 (nor_28_out, nor_27_out, and_159_out);
  nor nor_29 (nor_29_out, and_160_out, nor_30_out);
  nor nor_30 (nor_30_out, nor_29_out, and_161_out);
  nor nor_31 (nor_31_out, and_162_out, nor_32_out);
  nor nor_32 (nor_32_out, nor_31_out, and_163_out);
  nor nor_33 (nor_33_out, and_164_out, nor_34_out);
  nor nor_34 (nor_34_out, nor_33_out, and_165_out);
  nor nor_35 (nor_35_out, and_166_out, nor_36_out);
  nor nor_36 (nor_36_out, nor_35_out, and_167_out);
  nor nor_37 (nor_37_out, and_168_out, nor_38_out);
  nor nor_38 (nor_38_out, nor_37_out, and_169_out);
  or or_17 (or_17_out, MASTER_RST, and_170_out);
  nor nor_39 (nor_39_out, or_17_out, nor_40_out);
  nor nor_40 (nor_40_out, nor_39_out, and_171_out);
  and and_175 (and_175_out, and_87_out, and_131_out);
  or or_18 (or_18_out, and_175_out, and_173_out);
  assign ALUEO = and_135_out ? and_135_out : 1'bz;  // Driver driver_32
  assign ALUEBI = and_135_out ? and_135_out : 1'bz;  // Driver driver_33
  assign ALUEAI = and_135_out ? and_135_out : 1'bz;  // Driver driver_34
  assign ALOAD = and_135_out ? and_135_out : 1'bz;  // Driver driver_35
  assign ALUINVB = and_135_out ? and_135_out : 1'bz;  // Driver driver_36
  assign ALUCI = and_135_out ? and_135_out : 1'bz;  // Driver driver_37
  and and_176 (and_176_out, driver_102_out, not_2_out);
  not not_11 (not_11_out, or_46_out);
  and and_177 (and_177_out, and_88_out, and_131_out);
  and and_178 (and_178_out, MAN_OVERRIDE, MAN_D5);
  or or_19 (or_19_out, and_181_out, and_178_out);
  assign driver_38_out = and_99_out ? nor_7_out : 1'bz;  // Driver driver_38
  assign driver_38_out = and_101_out ? nor_9_out : 1'bz;  // Driver driver_39
  assign driver_38_out = and_103_out ? nor_11_out : 1'bz;  // Driver driver_40
  assign driver_38_out = and_105_out ? nor_13_out : 1'bz;  // Driver driver_41
  assign driver_38_out = and_107_out ? nor_15_out : 1'bz;  // Driver driver_42
  assign driver_38_out = and_109_out ? nor_17_out : 1'bz;  // Driver driver_43
  assign driver_38_out = and_111_out ? nor_19_out : 1'bz;  // Driver driver_44
  assign driver_38_out = and_113_out ? nor_21_out : 1'bz;  // Driver driver_45
  assign driver_38_out = and_115_out ? nor_23_out : 1'bz;  // Driver driver_46
  assign driver_38_out = and_117_out ? nor_25_out : 1'bz;  // Driver driver_47
  assign driver_38_out = and_119_out ? nor_27_out : 1'bz;  // Driver driver_48
  assign driver_38_out = and_121_out ? nor_29_out : 1'bz;  // Driver driver_49
  assign driver_38_out = and_123_out ? nor_31_out : 1'bz;  // Driver driver_50
  assign driver_38_out = and_125_out ? nor_33_out : 1'bz;  // Driver driver_51
  assign driver_38_out = and_127_out ? nor_35_out : 1'bz;  // Driver driver_52
  assign driver_38_out = and_129_out ? nor_37_out : 1'bz;  // Driver driver_53
  and and_179 (and_179_out, nor_39_out, not_1_out);
  and and_180 (and_180_out, and_89_out, and_131_out);
  and and_181 (and_181_out, driver_122_out, not_2_out);
  and and_182 (and_182_out, or_8_out, or_15_out);
  and and_183 (and_183_out, ~and_182_out, and_100_out);  // And
  and and_184 (and_184_out, and_100_out, and_182_out);
  and and_185 (and_185_out, ~and_182_out, and_102_out);  // And
  and and_186 (and_186_out, and_102_out, and_182_out);
  and and_187 (and_187_out, ~and_182_out, and_104_out);  // And
  and and_188 (and_188_out, and_104_out, and_182_out);
  and and_189 (and_189_out, ~and_182_out, and_106_out);  // And
  and and_190 (and_190_out, and_106_out, and_182_out);
  and and_191 (and_191_out, ~and_182_out, and_108_out);  // And
  and and_192 (and_192_out, and_108_out, and_182_out);
  and and_193 (and_193_out, ~and_182_out, and_110_out);  // And
  and and_194 (and_194_out, and_110_out, and_182_out);
  and and_195 (and_195_out, ~and_182_out, and_112_out);  // And
  and and_196 (and_196_out, and_112_out, and_182_out);
  and and_197 (and_197_out, ~and_182_out, and_114_out);  // And
  and and_198 (and_198_out, and_114_out, and_182_out);
  and and_199 (and_199_out, ~and_182_out, and_116_out);  // And
  and and_200 (and_200_out, and_116_out, and_182_out);
  and and_201 (and_201_out, ~and_182_out, and_118_out);  // And
  and and_202 (and_202_out, and_118_out, and_182_out);
  and and_203 (and_203_out, ~and_182_out, and_120_out);  // And
  and and_204 (and_204_out, and_120_out, and_182_out);
  and and_205 (and_205_out, ~and_182_out, and_122_out);  // And
  and and_206 (and_206_out, and_122_out, and_182_out);
  and and_207 (and_207_out, ~and_182_out, and_124_out);  // And
  and and_208 (and_208_out, and_124_out, and_182_out);
  and and_209 (and_209_out, ~and_182_out, and_126_out);  // And
  and and_210 (and_210_out, and_126_out, and_182_out);
  and and_211 (and_211_out, ~and_182_out, and_128_out);  // And
  and and_212 (and_212_out, and_128_out, and_182_out);
  and and_213 (and_213_out, ~and_182_out, and_130_out);  // And
  and and_214 (and_214_out, and_130_out, and_182_out);
  and and_215 (and_215_out, and_90_out, and_131_out);
  and and_216 (and_216_out, MAN_OVERRIDE, MAN_D6);
  or or_20 (or_20_out, and_217_out, and_216_out);
  nor nor_41 (nor_41_out, and_183_out, nor_42_out);
  nor nor_42 (nor_42_out, nor_41_out, and_184_out);
  nor nor_43 (nor_43_out, and_185_out, nor_44_out);
  nor nor_44 (nor_44_out, nor_43_out, and_186_out);
  nor nor_45 (nor_45_out, and_187_out, nor_46_out);
  nor nor_46 (nor_46_out, nor_45_out, and_188_out);
  nor nor_47 (nor_47_out, and_189_out, nor_48_out);
  nor nor_48 (nor_48_out, nor_47_out, and_190_out);
  nor nor_49 (nor_49_out, and_191_out, nor_50_out);
  nor nor_50 (nor_50_out, nor_49_out, and_192_out);
  nor nor_51 (nor_51_out, and_193_out, nor_52_out);
  nor nor_52 (nor_52_out, nor_51_out, and_194_out);
  nor nor_53 (nor_53_out, and_195_out, nor_54_out);
  nor nor_54 (nor_54_out, nor_53_out, and_196_out);
  nor nor_55 (nor_55_out, and_197_out, nor_56_out);
  nor nor_56 (nor_56_out, nor_55_out, and_198_out);
  nor nor_57 (nor_57_out, and_199_out, nor_58_out);
  nor nor_58 (nor_58_out, nor_57_out, and_200_out);
  nor nor_59 (nor_59_out, and_201_out, nor_60_out);
  nor nor_60 (nor_60_out, nor_59_out, and_202_out);
  nor nor_61 (nor_61_out, and_203_out, nor_62_out);
  nor nor_62 (nor_62_out, nor_61_out, and_204_out);
  nor nor_63 (nor_63_out, and_205_out, nor_64_out);
  nor nor_64 (nor_64_out, nor_63_out, and_206_out);
  nor nor_65 (nor_65_out, and_207_out, nor_66_out);
  nor nor_66 (nor_66_out, nor_65_out, and_208_out);
  nor nor_67 (nor_67_out, and_209_out, nor_68_out);
  nor nor_68 (nor_68_out, nor_67_out, and_210_out);
  nor nor_69 (nor_69_out, and_211_out, nor_70_out);
  nor nor_70 (nor_70_out, nor_69_out, and_212_out);
  nor nor_71 (nor_71_out, and_213_out, nor_72_out);
  nor nor_72 (nor_72_out, nor_71_out, and_214_out);
  and and_217 (and_217_out, driver_146_out, not_2_out);
  and and_218 (and_218_out, MAN_OVERRIDE, MAN_D7);
  or or_21 (or_21_out, and_220_out, and_218_out);
  assign driver_54_out = and_99_out ? nor_41_out : 1'bz;  // Driver driver_54
  assign driver_54_out = and_101_out ? nor_43_out : 1'bz;  // Driver driver_55
  assign driver_54_out = and_103_out ? nor_45_out : 1'bz;  // Driver driver_56
  assign driver_54_out = and_105_out ? nor_47_out : 1'bz;  // Driver driver_57
  assign driver_54_out = and_107_out ? nor_49_out : 1'bz;  // Driver driver_58
  assign driver_54_out = and_109_out ? nor_51_out : 1'bz;  // Driver driver_59
  assign driver_54_out = and_111_out ? nor_53_out : 1'bz;  // Driver driver_60
  assign driver_54_out = and_113_out ? nor_55_out : 1'bz;  // Driver driver_61
  assign driver_54_out = and_115_out ? nor_57_out : 1'bz;  // Driver driver_62
  assign driver_54_out = and_117_out ? nor_59_out : 1'bz;  // Driver driver_63
  assign driver_54_out = and_119_out ? nor_61_out : 1'bz;  // Driver driver_64
  assign driver_54_out = and_121_out ? nor_63_out : 1'bz;  // Driver driver_65
  assign driver_54_out = and_123_out ? nor_65_out : 1'bz;  // Driver driver_66
  assign driver_54_out = and_125_out ? nor_67_out : 1'bz;  // Driver driver_67
  assign driver_54_out = and_127_out ? nor_69_out : 1'bz;  // Driver driver_68
  assign driver_54_out = and_129_out ? nor_71_out : 1'bz;  // Driver driver_69
  and and_219 (and_219_out, and_80_out, and_179_out);
  and and_220 (and_220_out, driver_162_out, not_2_out);
  and and_221 (and_221_out, or_13_out, or_15_out);
  and and_222 (and_222_out, ~and_221_out, and_100_out);  // And
  and and_223 (and_223_out, and_100_out, and_221_out);
  and and_224 (and_224_out, ~and_221_out, and_102_out);  // And
  and and_225 (and_225_out, and_102_out, and_221_out);
  and and_226 (and_226_out, ~and_221_out, and_104_out);  // And
  and and_227 (and_227_out, and_104_out, and_221_out);
  and and_228 (and_228_out, ~and_221_out, and_106_out);  // And
  and and_229 (and_229_out, and_106_out, and_221_out);
  and and_230 (and_230_out, ~and_221_out, and_108_out);  // And
  and and_231 (and_231_out, and_108_out, and_221_out);
  and and_232 (and_232_out, ~and_221_out, and_110_out);  // And
  and and_233 (and_233_out, and_110_out, and_221_out);
  and and_234 (and_234_out, ~and_221_out, and_112_out);  // And
  and and_235 (and_235_out, and_112_out, and_221_out);
  and and_236 (and_236_out, ~and_221_out, and_114_out);  // And
  and and_237 (and_237_out, and_114_out, and_221_out);
  and and_238 (and_238_out, ~and_221_out, and_116_out);  // And
  and and_239 (and_239_out, and_116_out, and_221_out);
  and and_240 (and_240_out, ~and_221_out, and_118_out);  // And
  and and_241 (and_241_out, and_118_out, and_221_out);
  and and_242 (and_242_out, ~and_221_out, and_120_out);  // And
  and and_243 (and_243_out, and_120_out, and_221_out);
  and and_244 (and_244_out, ~and_221_out, and_122_out);  // And
  and and_245 (and_245_out, and_122_out, and_221_out);
  and and_246 (and_246_out, ~and_221_out, and_124_out);  // And
  and and_247 (and_247_out, and_124_out, and_221_out);
  and and_248 (and_248_out, ~and_221_out, and_126_out);  // And
  and and_249 (and_249_out, and_126_out, and_221_out);
  and and_250 (and_250_out, ~and_221_out, and_128_out);  // And
  and and_251 (and_251_out, and_128_out, and_221_out);
  and and_252 (and_252_out, ~and_221_out, and_130_out);  // And
  and and_253 (and_253_out, and_130_out, and_221_out);
  and and_254 (and_254_out, and_81_out, and_179_out);
  nor nor_73 (nor_73_out, and_222_out, nor_74_out);
  nor nor_74 (nor_74_out, nor_73_out, and_223_out);
  nor nor_75 (nor_75_out, and_224_out, nor_76_out);
  nor nor_76 (nor_76_out, nor_75_out, and_225_out);
  nor nor_77 (nor_77_out, and_226_out, nor_78_out);
  nor nor_78 (nor_78_out, nor_77_out, and_227_out);
  nor nor_79 (nor_79_out, and_228_out, nor_80_out);
  nor nor_80 (nor_80_out, nor_79_out, and_229_out);
  nor nor_81 (nor_81_out, and_230_out, nor_82_out);
  nor nor_82 (nor_82_out, nor_81_out, and_231_out);
  nor nor_83 (nor_83_out, and_232_out, nor_84_out);
  nor nor_84 (nor_84_out, nor_83_out, and_233_out);
  nor nor_85 (nor_85_out, and_234_out, nor_86_out);
  nor nor_86 (nor_86_out, nor_85_out, and_235_out);
  nor nor_87 (nor_87_out, and_236_out, nor_88_out);
  nor nor_88 (nor_88_out, nor_87_out, and_237_out);
  nor nor_89 (nor_89_out, and_238_out, nor_90_out);
  nor nor_90 (nor_90_out, nor_89_out, and_239_out);
  nor nor_91 (nor_91_out, and_240_out, nor_92_out);
  nor nor_92 (nor_92_out, nor_91_out, and_241_out);
  nor nor_93 (nor_93_out, and_242_out, nor_94_out);
  nor nor_94 (nor_94_out, nor_93_out, and_243_out);
  nor nor_95 (nor_95_out, and_244_out, nor_96_out);
  nor nor_96 (nor_96_out, nor_95_out, and_245_out);
  nor nor_97 (nor_97_out, and_246_out, nor_98_out);
  nor nor_98 (nor_98_out, nor_97_out, and_247_out);
  nor nor_99 (nor_99_out, and_248_out, nor_100_out);
  nor nor_100 (nor_100_out, nor_99_out, and_249_out);
  nor nor_101 (nor_101_out, and_250_out, nor_102_out);
  nor nor_102 (nor_102_out, nor_101_out, and_251_out);
  nor nor_103 (nor_103_out, and_252_out, nor_104_out);
  nor nor_104 (nor_104_out, nor_103_out, and_253_out);
  and and_255 (and_255_out, and_86_out, and_179_out);
  assign driver_70_out = and_99_out ? nor_73_out : 1'bz;  // Driver driver_70
  assign driver_70_out = and_101_out ? nor_75_out : 1'bz;  // Driver driver_71
  assign driver_70_out = and_103_out ? nor_77_out : 1'bz;  // Driver driver_72
  assign driver_70_out = and_105_out ? nor_79_out : 1'bz;  // Driver driver_73
  assign driver_70_out = and_107_out ? nor_81_out : 1'bz;  // Driver driver_74
  assign driver_70_out = and_109_out ? nor_83_out : 1'bz;  // Driver driver_75
  assign driver_70_out = and_111_out ? nor_85_out : 1'bz;  // Driver driver_76
  assign driver_70_out = and_113_out ? nor_87_out : 1'bz;  // Driver driver_77
  assign driver_70_out = and_115_out ? nor_89_out : 1'bz;  // Driver driver_78
  assign driver_70_out = and_117_out ? nor_91_out : 1'bz;  // Driver driver_79
  assign driver_70_out = and_119_out ? nor_93_out : 1'bz;  // Driver driver_80
  assign driver_70_out = and_121_out ? nor_95_out : 1'bz;  // Driver driver_81
  assign driver_70_out = and_123_out ? nor_97_out : 1'bz;  // Driver driver_82
  assign driver_70_out = and_125_out ? nor_99_out : 1'bz;  // Driver driver_83
  assign driver_70_out = and_127_out ? nor_101_out : 1'bz;  // Driver driver_84
  assign driver_70_out = and_129_out ? nor_103_out : 1'bz;  // Driver driver_85
  and and_256 (and_256_out, and_87_out, and_179_out);
  and and_257 (and_257_out, or_14_out, or_15_out);
  and and_258 (and_258_out, ~and_257_out, and_100_out);  // And
  and and_259 (and_259_out, and_100_out, and_257_out);
  and and_260 (and_260_out, ~and_257_out, and_102_out);  // And
  and and_261 (and_261_out, and_102_out, and_257_out);
  and and_262 (and_262_out, ~and_257_out, and_104_out);  // And
  and and_263 (and_263_out, and_104_out, and_257_out);
  and and_264 (and_264_out, ~and_257_out, and_106_out);  // And
  and and_265 (and_265_out, and_106_out, and_257_out);
  and and_266 (and_266_out, ~and_257_out, and_108_out);  // And
  and and_267 (and_267_out, and_108_out, and_257_out);
  and and_268 (and_268_out, ~and_257_out, and_110_out);  // And
  and and_269 (and_269_out, and_110_out, and_257_out);
  and and_270 (and_270_out, ~and_257_out, and_112_out);  // And
  and and_271 (and_271_out, and_112_out, and_257_out);
  and and_272 (and_272_out, ~and_257_out, and_114_out);  // And
  and and_273 (and_273_out, and_114_out, and_257_out);
  and and_274 (and_274_out, ~and_257_out, and_116_out);  // And
  and and_275 (and_275_out, and_116_out, and_257_out);
  and and_276 (and_276_out, ~and_257_out, and_118_out);  // And
  and and_277 (and_277_out, and_118_out, and_257_out);
  and and_278 (and_278_out, ~and_257_out, and_120_out);  // And
  and and_279 (and_279_out, and_120_out, and_257_out);
  and and_280 (and_280_out, ~and_257_out, and_122_out);  // And
  and and_281 (and_281_out, and_122_out, and_257_out);
  and and_282 (and_282_out, ~and_257_out, and_124_out);  // And
  and and_283 (and_283_out, and_124_out, and_257_out);
  and and_284 (and_284_out, ~and_257_out, and_126_out);  // And
  and and_285 (and_285_out, and_126_out, and_257_out);
  and and_286 (and_286_out, ~and_257_out, and_128_out);  // And
  and and_287 (and_287_out, and_128_out, and_257_out);
  and and_288 (and_288_out, ~and_257_out, and_130_out);  // And
  and and_289 (and_289_out, and_130_out, and_257_out);
  nor nor_105 (nor_105_out, and_258_out, nor_106_out);
  nor nor_106 (nor_106_out, nor_105_out, and_259_out);
  nor nor_107 (nor_107_out, and_260_out, nor_108_out);
  nor nor_108 (nor_108_out, nor_107_out, and_261_out);
  nor nor_109 (nor_109_out, and_262_out, nor_110_out);
  nor nor_110 (nor_110_out, nor_109_out, and_263_out);
  nor nor_111 (nor_111_out, and_264_out, nor_112_out);
  nor nor_112 (nor_112_out, nor_111_out, and_265_out);
  nor nor_113 (nor_113_out, and_266_out, nor_114_out);
  nor nor_114 (nor_114_out, nor_113_out, and_267_out);
  nor nor_115 (nor_115_out, and_268_out, nor_116_out);
  nor nor_116 (nor_116_out, nor_115_out, and_269_out);
  nor nor_117 (nor_117_out, and_270_out, nor_118_out);
  nor nor_118 (nor_118_out, nor_117_out, and_271_out);
  nor nor_119 (nor_119_out, and_272_out, nor_120_out);
  nor nor_120 (nor_120_out, nor_119_out, and_273_out);
  nor nor_121 (nor_121_out, and_274_out, nor_122_out);
  nor nor_122 (nor_122_out, nor_121_out, and_275_out);
  nor nor_123 (nor_123_out, and_276_out, nor_124_out);
  nor nor_124 (nor_124_out, nor_123_out, and_277_out);
  nor nor_125 (nor_125_out, and_278_out, nor_126_out);
  nor nor_126 (nor_126_out, nor_125_out, and_279_out);
  nor nor_127 (nor_127_out, and_280_out, nor_128_out);
  nor nor_128 (nor_128_out, nor_127_out, and_281_out);
  nor nor_129 (nor_129_out, and_282_out, nor_130_out);
  nor nor_130 (nor_130_out, nor_129_out, and_283_out);
  nor nor_131 (nor_131_out, and_284_out, nor_132_out);
  nor nor_132 (nor_132_out, nor_131_out, and_285_out);
  nor nor_133 (nor_133_out, and_286_out, nor_134_out);
  nor nor_134 (nor_134_out, nor_133_out, and_287_out);
  nor nor_135 (nor_135_out, and_288_out, nor_136_out);
  nor nor_136 (nor_136_out, nor_135_out, and_289_out);
  not not_12 (not_12_out, or_46_out);
  not not_13 (not_13_out, not_12_out);
  assign driver_86_out = and_99_out ? nor_105_out : 1'bz;  // Driver driver_86
  assign driver_86_out = and_101_out ? nor_107_out : 1'bz;  // Driver driver_87
  assign driver_86_out = and_103_out ? nor_109_out : 1'bz;  // Driver driver_88
  assign driver_86_out = and_105_out ? nor_111_out : 1'bz;  // Driver driver_89
  assign driver_86_out = and_107_out ? nor_113_out : 1'bz;  // Driver driver_90
  assign driver_86_out = and_109_out ? nor_115_out : 1'bz;  // Driver driver_91
  assign driver_86_out = and_111_out ? nor_117_out : 1'bz;  // Driver driver_92
  assign driver_86_out = and_113_out ? nor_119_out : 1'bz;  // Driver driver_93
  assign driver_86_out = and_115_out ? nor_121_out : 1'bz;  // Driver driver_94
  assign driver_86_out = and_117_out ? nor_123_out : 1'bz;  // Driver driver_95
  assign driver_86_out = and_119_out ? nor_125_out : 1'bz;  // Driver driver_96
  assign driver_86_out = and_121_out ? nor_127_out : 1'bz;  // Driver driver_97
  assign driver_86_out = and_123_out ? nor_129_out : 1'bz;  // Driver driver_98
  assign driver_86_out = and_125_out ? nor_131_out : 1'bz;  // Driver driver_99
  assign driver_86_out = and_127_out ? nor_133_out : 1'bz;  // Driver driver_100
  assign driver_86_out = and_129_out ? nor_135_out : 1'bz;  // Driver driver_101
  and and_290 (and_290_out, or_46_out, ~not_13_out);  // And
  and and_291 (and_291_out, or_16_out, or_15_out);
  and and_292 (and_292_out, ~and_291_out, and_100_out);  // And
  and and_293 (and_293_out, and_100_out, and_291_out);
  and and_294 (and_294_out, ~and_291_out, and_102_out);  // And
  and and_295 (and_295_out, and_102_out, and_291_out);
  and and_296 (and_296_out, ~and_291_out, and_104_out);  // And
  and and_297 (and_297_out, and_104_out, and_291_out);
  and and_298 (and_298_out, ~and_291_out, and_106_out);  // And
  and and_299 (and_299_out, and_106_out, and_291_out);
  and and_300 (and_300_out, ~and_291_out, and_108_out);  // And
  and and_301 (and_301_out, and_108_out, and_291_out);
  and and_302 (and_302_out, ~and_291_out, and_110_out);  // And
  and and_303 (and_303_out, and_110_out, and_291_out);
  and and_304 (and_304_out, ~and_291_out, and_112_out);  // And
  and and_305 (and_305_out, and_112_out, and_291_out);
  and and_306 (and_306_out, ~and_291_out, and_114_out);  // And
  and and_307 (and_307_out, and_114_out, and_291_out);
  and and_308 (and_308_out, ~and_291_out, and_116_out);  // And
  and and_309 (and_309_out, and_116_out, and_291_out);
  and and_310 (and_310_out, ~and_291_out, and_118_out);  // And
  and and_311 (and_311_out, and_118_out, and_291_out);
  and and_312 (and_312_out, ~and_291_out, and_120_out);  // And
  and and_313 (and_313_out, and_120_out, and_291_out);
  and and_314 (and_314_out, ~and_291_out, and_122_out);  // And
  and and_315 (and_315_out, and_122_out, and_291_out);
  and and_316 (and_316_out, ~and_291_out, and_124_out);  // And
  and and_317 (and_317_out, and_124_out, and_291_out);
  and and_318 (and_318_out, ~and_291_out, and_126_out);  // And
  and and_319 (and_319_out, and_126_out, and_291_out);
  and and_320 (and_320_out, ~and_291_out, and_128_out);  // And
  and and_321 (and_321_out, and_128_out, and_291_out);
  and and_322 (and_322_out, ~and_291_out, and_130_out);  // And
  and and_323 (and_323_out, and_130_out, and_291_out);
  not not_14 (not_14_out, or_46_out);
  not not_15 (not_15_out, not_14_out);
  not not_16 (not_16_out, MARLOAD);
  and and_324 (and_324_out, MARLOAD, driver_38_out);
  or or_22 (or_22_out, and_329_out, and_324_out);
  and and_325 (and_325_out, MARLOAD, driver_54_out);
  or or_23 (or_23_out, and_330_out, and_325_out);
  and and_326 (and_326_out, MARLOAD, driver_70_out);
  or or_24 (or_24_out, and_331_out, and_326_out);
  and and_327 (and_327_out, MARLOAD, driver_86_out);
  or or_25 (or_25_out, and_332_out, and_327_out);
  nor nor_137 (nor_137_out, and_292_out, nor_138_out);
  nor nor_138 (nor_138_out, nor_137_out, and_293_out);
  nor nor_139 (nor_139_out, and_294_out, nor_140_out);
  nor nor_140 (nor_140_out, nor_139_out, and_295_out);
  nor nor_141 (nor_141_out, and_296_out, nor_142_out);
  nor nor_142 (nor_142_out, nor_141_out, and_297_out);
  nor nor_143 (nor_143_out, and_298_out, nor_144_out);
  nor nor_144 (nor_144_out, nor_143_out, and_299_out);
  nor nor_145 (nor_145_out, and_300_out, nor_146_out);
  nor nor_146 (nor_146_out, nor_145_out, and_301_out);
  nor nor_147 (nor_147_out, and_302_out, nor_148_out);
  nor nor_148 (nor_148_out, nor_147_out, and_303_out);
  nor nor_149 (nor_149_out, and_304_out, nor_150_out);
  nor nor_150 (nor_150_out, nor_149_out, and_305_out);
  nor nor_151 (nor_151_out, and_306_out, nor_152_out);
  nor nor_152 (nor_152_out, nor_151_out, and_307_out);
  nor nor_153 (nor_153_out, and_308_out, nor_154_out);
  nor nor_154 (nor_154_out, nor_153_out, and_309_out);
  nor nor_155 (nor_155_out, and_310_out, nor_156_out);
  nor nor_156 (nor_156_out, nor_155_out, and_311_out);
  nor nor_157 (nor_157_out, and_312_out, nor_158_out);
  nor nor_158 (nor_158_out, nor_157_out, and_313_out);
  nor nor_159 (nor_159_out, and_314_out, nor_160_out);
  nor nor_160 (nor_160_out, nor_159_out, and_315_out);
  nor nor_161 (nor_161_out, and_316_out, nor_162_out);
  nor nor_162 (nor_162_out, nor_161_out, and_317_out);
  nor nor_163 (nor_163_out, and_318_out, nor_164_out);
  nor nor_164 (nor_164_out, nor_163_out, and_319_out);
  nor nor_165 (nor_165_out, and_320_out, nor_166_out);
  nor nor_166 (nor_166_out, nor_165_out, and_321_out);
  nor nor_167 (nor_167_out, and_322_out, nor_168_out);
  nor nor_168 (nor_168_out, nor_167_out, and_323_out);
  and and_328 (and_328_out, or_46_out, ~not_15_out);  // And
  and and_329 (and_329_out, nor_169_out, not_16_out);
  and and_330 (and_330_out, nor_171_out, not_16_out);
  and and_331 (and_331_out, nor_173_out, not_16_out);
  and and_332 (and_332_out, nor_175_out, not_16_out);
  not not_17 (not_17_out, IRLOAD);
  and and_333 (and_333_out, IRLOAD, driver_38_out);
  or or_26 (or_26_out, and_349_out, and_333_out);
  and and_334 (and_334_out, IRLOAD, driver_54_out);
  or or_27 (or_27_out, and_350_out, and_334_out);
  and and_335 (and_335_out, IRLOAD, driver_70_out);
  or or_28 (or_28_out, and_351_out, and_335_out);
  and and_336 (and_336_out, IRLOAD, driver_86_out);
  or or_29 (or_29_out, and_352_out, and_336_out);
  and and_337 (and_337_out, IRLOAD, driver_102_out);
  or or_30 (or_30_out, and_353_out, and_337_out);
  and and_338 (and_338_out, IRLOAD, driver_122_out);
  or or_31 (or_31_out, and_354_out, and_338_out);
  and and_339 (and_339_out, IRLOAD, driver_146_out);
  or or_32 (or_32_out, and_355_out, and_339_out);
  and and_340 (and_340_out, IRLOAD, driver_162_out);
  or or_33 (or_33_out, and_356_out, and_340_out);
  and and_341 (and_341_out, ~or_22_out, and_290_out);  // And
  and and_342 (and_342_out, and_290_out, or_22_out);
  and and_343 (and_343_out, ~or_23_out, and_290_out);  // And
  and and_344 (and_344_out, and_290_out, or_23_out);
  and and_345 (and_345_out, ~or_24_out, and_290_out);  // And
  and and_346 (and_346_out, and_290_out, or_24_out);
  and and_347 (and_347_out, ~or_25_out, and_290_out);  // And
  and and_348 (and_348_out, and_290_out, or_25_out);
  assign driver_102_out = and_99_out ? nor_137_out : 1'bz;  // Driver driver_102
  assign driver_102_out = and_101_out ? nor_139_out : 1'bz;  // Driver driver_103
  assign driver_102_out = and_103_out ? nor_141_out : 1'bz;  // Driver driver_104
  assign driver_102_out = and_105_out ? nor_143_out : 1'bz;  // Driver driver_105
  assign driver_102_out = and_107_out ? nor_145_out : 1'bz;  // Driver driver_106
  assign driver_102_out = and_109_out ? nor_147_out : 1'bz;  // Driver driver_107
  assign driver_102_out = and_111_out ? nor_149_out : 1'bz;  // Driver driver_108
  assign driver_102_out = and_113_out ? nor_151_out : 1'bz;  // Driver driver_109
  assign driver_102_out = and_115_out ? nor_153_out : 1'bz;  // Driver driver_110
  assign driver_102_out = and_117_out ? nor_155_out : 1'bz;  // Driver driver_111
  assign driver_102_out = and_119_out ? nor_157_out : 1'bz;  // Driver driver_112
  assign driver_102_out = and_121_out ? nor_159_out : 1'bz;  // Driver driver_113
  assign driver_102_out = and_123_out ? nor_161_out : 1'bz;  // Driver driver_114
  assign driver_102_out = and_125_out ? nor_163_out : 1'bz;  // Driver driver_115
  assign driver_102_out = and_127_out ? nor_165_out : 1'bz;  // Driver driver_116
  assign driver_102_out = and_129_out ? nor_167_out : 1'bz;  // Driver driver_117
  and and_349 (and_349_out, nor_209_out, not_17_out);
  and and_350 (and_350_out, nor_211_out, not_17_out);
  and and_351 (and_351_out, nor_213_out, not_17_out);
  and and_352 (and_352_out, nor_215_out, not_17_out);
  and and_353 (and_353_out, nor_217_out, not_17_out);
  and and_354 (and_354_out, nor_219_out, not_17_out);
  and and_355 (and_355_out, nor_221_out, not_17_out);
  and and_356 (and_356_out, nor_223_out, not_17_out);
  or or_34 (or_34_out, MARCLR, and_341_out);
  nor nor_169 (nor_169_out, or_34_out, nor_170_out);
  nor nor_170 (nor_170_out, nor_169_out, and_342_out);
  or or_35 (or_35_out, MARCLR, and_343_out);
  nor nor_171 (nor_171_out, or_35_out, nor_172_out);
  nor nor_172 (nor_172_out, nor_171_out, and_344_out);
  or or_36 (or_36_out, MARCLR, and_345_out);
  nor nor_173 (nor_173_out, or_36_out, nor_174_out);
  nor nor_174 (nor_174_out, nor_173_out, and_346_out);
  or or_37 (or_37_out, MARCLR, and_347_out);
  nor nor_175 (nor_175_out, or_37_out, nor_176_out);
  nor nor_176 (nor_176_out, nor_175_out, and_348_out);
  and and_357 (and_357_out, or_19_out, or_15_out);
  and and_358 (and_358_out, ~and_357_out, and_100_out);  // And
  and and_359 (and_359_out, and_100_out, and_357_out);
  and and_360 (and_360_out, ~and_357_out, and_102_out);  // And
  and and_361 (and_361_out, and_102_out, and_357_out);
  and and_362 (and_362_out, ~and_357_out, and_104_out);  // And
  and and_363 (and_363_out, and_104_out, and_357_out);
  and and_364 (and_364_out, ~and_357_out, and_106_out);  // And
  and and_365 (and_365_out, and_106_out, and_357_out);
  and and_366 (and_366_out, ~and_357_out, and_108_out);  // And
  and and_367 (and_367_out, and_108_out, and_357_out);
  and and_368 (and_368_out, ~and_357_out, and_110_out);  // And
  and and_369 (and_369_out, and_110_out, and_357_out);
  and and_370 (and_370_out, ~and_357_out, and_112_out);  // And
  and and_371 (and_371_out, and_112_out, and_357_out);
  and and_372 (and_372_out, ~and_357_out, and_114_out);  // And
  and and_373 (and_373_out, and_114_out, and_357_out);
  and and_374 (and_374_out, ~and_357_out, and_116_out);  // And
  and and_375 (and_375_out, and_116_out, and_357_out);
  and and_376 (and_376_out, ~and_357_out, and_118_out);  // And
  and and_377 (and_377_out, and_118_out, and_357_out);
  and and_378 (and_378_out, ~and_357_out, and_120_out);  // And
  and and_379 (and_379_out, and_120_out, and_357_out);
  and and_380 (and_380_out, ~and_357_out, and_122_out);  // And
  and and_381 (and_381_out, and_122_out, and_357_out);
  and and_382 (and_382_out, ~and_357_out, and_124_out);  // And
  and and_383 (and_383_out, and_124_out, and_357_out);
  and and_384 (and_384_out, ~and_357_out, and_126_out);  // And
  and and_385 (and_385_out, and_126_out, and_357_out);
  and and_386 (and_386_out, ~and_357_out, and_128_out);  // And
  and and_387 (and_387_out, and_128_out, and_357_out);
  and and_388 (and_388_out, ~and_357_out, and_130_out);  // And
  and and_389 (and_389_out, and_130_out, and_357_out);
  and and_390 (and_390_out, ~or_26_out, and_328_out);  // And
  and and_391 (and_391_out, and_328_out, or_26_out);
  and and_392 (and_392_out, ~or_27_out, and_328_out);  // And
  and and_393 (and_393_out, and_328_out, or_27_out);
  and and_394 (and_394_out, ~or_28_out, and_328_out);  // And
  and and_395 (and_395_out, and_328_out, or_28_out);
  and and_396 (and_396_out, ~or_29_out, and_328_out);  // And
  and and_397 (and_397_out, and_328_out, or_29_out);
  and and_398 (and_398_out, ~or_30_out, and_328_out);  // And
  and and_399 (and_399_out, and_328_out, or_30_out);
  and and_400 (and_400_out, ~or_31_out, and_328_out);  // And
  and and_401 (and_401_out, and_328_out, or_31_out);
  and and_402 (and_402_out, ~or_32_out, and_328_out);  // And
  and and_403 (and_403_out, and_328_out, or_32_out);
  and and_404 (and_404_out, ~or_33_out, and_328_out);  // And
  and and_405 (and_405_out, and_328_out, or_33_out);
  nor nor_177 (nor_177_out, and_358_out, nor_178_out);
  nor nor_178 (nor_178_out, nor_177_out, and_359_out);
  nor nor_179 (nor_179_out, and_360_out, nor_180_out);
  nor nor_180 (nor_180_out, nor_179_out, and_361_out);
  nor nor_181 (nor_181_out, and_362_out, nor_182_out);
  nor nor_182 (nor_182_out, nor_181_out, and_363_out);
  nor nor_183 (nor_183_out, and_364_out, nor_184_out);
  nor nor_184 (nor_184_out, nor_183_out, and_365_out);
  nor nor_185 (nor_185_out, and_366_out, nor_186_out);
  nor nor_186 (nor_186_out, nor_185_out, and_367_out);
  nor nor_187 (nor_187_out, and_368_out, nor_188_out);
  nor nor_188 (nor_188_out, nor_187_out, and_369_out);
  nor nor_189 (nor_189_out, and_370_out, nor_190_out);
  nor nor_190 (nor_190_out, nor_189_out, and_371_out);
  nor nor_191 (nor_191_out, and_372_out, nor_192_out);
  nor nor_192 (nor_192_out, nor_191_out, and_373_out);
  nor nor_193 (nor_193_out, and_374_out, nor_194_out);
  nor nor_194 (nor_194_out, nor_193_out, and_375_out);
  nor nor_195 (nor_195_out, and_376_out, nor_196_out);
  nor nor_196 (nor_196_out, nor_195_out, and_377_out);
  nor nor_197 (nor_197_out, and_378_out, nor_198_out);
  nor nor_198 (nor_198_out, nor_197_out, and_379_out);
  nor nor_199 (nor_199_out, and_380_out, nor_200_out);
  nor nor_200 (nor_200_out, nor_199_out, and_381_out);
  nor nor_201 (nor_201_out, and_382_out, nor_202_out);
  nor nor_202 (nor_202_out, nor_201_out, and_383_out);
  nor nor_203 (nor_203_out, and_384_out, nor_204_out);
  nor nor_204 (nor_204_out, nor_203_out, and_385_out);
  nor nor_205 (nor_205_out, and_386_out, nor_206_out);
  nor nor_206 (nor_206_out, nor_205_out, and_387_out);
  nor nor_207 (nor_207_out, and_388_out, nor_208_out);
  nor nor_208 (nor_208_out, nor_207_out, and_389_out);
  or or_38 (or_38_out, IRCLR, and_390_out);
  nor nor_209 (nor_209_out, or_38_out, nor_210_out);
  nor nor_210 (nor_210_out, nor_209_out, and_391_out);
  or or_39 (or_39_out, IRCLR, and_392_out);
  nor nor_211 (nor_211_out, or_39_out, nor_212_out);
  nor nor_212 (nor_212_out, nor_211_out, and_393_out);
  or or_40 (or_40_out, IRCLR, and_394_out);
  nor nor_213 (nor_213_out, or_40_out, nor_214_out);
  nor nor_214 (nor_214_out, nor_213_out, and_395_out);
  or or_41 (or_41_out, IRCLR, and_396_out);
  nor nor_215 (nor_215_out, or_41_out, nor_216_out);
  nor nor_216 (nor_216_out, nor_215_out, and_397_out);
  or or_42 (or_42_out, IRCLR, and_398_out);
  nor nor_217 (nor_217_out, or_42_out, nor_218_out);
  nor nor_218 (nor_218_out, nor_217_out, and_399_out);
  or or_43 (or_43_out, IRCLR, and_400_out);
  nor nor_219 (nor_219_out, or_43_out, nor_220_out);
  nor nor_220 (nor_220_out, nor_219_out, and_401_out);
  or or_44 (or_44_out, IRCLR, and_402_out);
  nor nor_221 (nor_221_out, or_44_out, nor_222_out);
  nor nor_222 (nor_222_out, nor_221_out, and_403_out);
  or or_45 (or_45_out, IRCLR, and_404_out);
  nor nor_223 (nor_223_out, or_45_out, nor_224_out);
  nor nor_224 (nor_224_out, nor_223_out, and_405_out);
  assign driver_38_out = MARO ? nor_169_out : 1'bz;  // Driver driver_118
  assign driver_54_out = MARO ? nor_171_out : 1'bz;  // Driver driver_119
  assign driver_70_out = MARO ? nor_173_out : 1'bz;  // Driver driver_120
  assign driver_86_out = MARO ? nor_175_out : 1'bz;  // Driver driver_121
  assign driver_122_out = and_99_out ? nor_177_out : 1'bz;  // Driver driver_122
  assign driver_122_out = and_101_out ? nor_179_out : 1'bz;  // Driver driver_123
  assign driver_122_out = and_103_out ? nor_181_out : 1'bz;  // Driver driver_124
  assign driver_122_out = and_105_out ? nor_183_out : 1'bz;  // Driver driver_125
  assign driver_122_out = and_107_out ? nor_185_out : 1'bz;  // Driver driver_126
  assign driver_122_out = and_109_out ? nor_187_out : 1'bz;  // Driver driver_127
  assign driver_122_out = and_111_out ? nor_189_out : 1'bz;  // Driver driver_128
  assign driver_122_out = and_113_out ? nor_191_out : 1'bz;  // Driver driver_129
  assign driver_122_out = and_115_out ? nor_193_out : 1'bz;  // Driver driver_130
  assign driver_122_out = and_117_out ? nor_195_out : 1'bz;  // Driver driver_131
  assign driver_122_out = and_119_out ? nor_197_out : 1'bz;  // Driver driver_132
  assign driver_122_out = and_121_out ? nor_199_out : 1'bz;  // Driver driver_133
  assign driver_122_out = and_123_out ? nor_201_out : 1'bz;  // Driver driver_134
  assign driver_122_out = and_125_out ? nor_203_out : 1'bz;  // Driver driver_135
  assign driver_122_out = and_127_out ? nor_205_out : 1'bz;  // Driver driver_136
  assign driver_122_out = and_129_out ? nor_207_out : 1'bz;  // Driver driver_137
  and and_406 (and_406_out, or_20_out, or_15_out);
  and and_407 (and_407_out, ~and_406_out, and_100_out);  // And
  and and_408 (and_408_out, and_100_out, and_406_out);
  and and_409 (and_409_out, ~and_406_out, and_102_out);  // And
  and and_410 (and_410_out, and_102_out, and_406_out);
  and and_411 (and_411_out, ~and_406_out, and_104_out);  // And
  and and_412 (and_412_out, and_104_out, and_406_out);
  and and_413 (and_413_out, ~and_406_out, and_106_out);  // And
  and and_414 (and_414_out, and_106_out, and_406_out);
  and and_415 (and_415_out, ~and_406_out, and_108_out);  // And
  and and_416 (and_416_out, and_108_out, and_406_out);
  and and_417 (and_417_out, ~and_406_out, and_110_out);  // And
  and and_418 (and_418_out, and_110_out, and_406_out);
  and and_419 (and_419_out, ~and_406_out, and_112_out);  // And
  and and_420 (and_420_out, and_112_out, and_406_out);
  and and_421 (and_421_out, ~and_406_out, and_114_out);  // And
  and and_422 (and_422_out, and_114_out, and_406_out);
  and and_423 (and_423_out, ~and_406_out, and_116_out);  // And
  and and_424 (and_424_out, and_116_out, and_406_out);
  and and_425 (and_425_out, ~and_406_out, and_118_out);  // And
  and and_426 (and_426_out, and_118_out, and_406_out);
  and and_427 (and_427_out, ~and_406_out, and_120_out);  // And
  and and_428 (and_428_out, and_120_out, and_406_out);
  and and_429 (and_429_out, ~and_406_out, and_122_out);  // And
  and and_430 (and_430_out, and_122_out, and_406_out);
  and and_431 (and_431_out, ~and_406_out, and_124_out);  // And
  and and_432 (and_432_out, and_124_out, and_406_out);
  and and_433 (and_433_out, ~and_406_out, and_126_out);  // And
  and and_434 (and_434_out, and_126_out, and_406_out);
  and and_435 (and_435_out, ~and_406_out, and_128_out);  // And
  and and_436 (and_436_out, and_128_out, and_406_out);
  and and_437 (and_437_out, ~and_406_out, and_130_out);  // And
  and and_438 (and_438_out, and_130_out, and_406_out);
  assign driver_38_out = IREO ? nor_209_out : 1'bz;  // Driver driver_138
  assign driver_54_out = IREO ? nor_211_out : 1'bz;  // Driver driver_139
  assign driver_70_out = IREO ? nor_213_out : 1'bz;  // Driver driver_140
  assign driver_86_out = IREO ? nor_215_out : 1'bz;  // Driver driver_141
  Driver driver_142 (.in(nor_217_out), .en(IREO));  // open: out
  Driver driver_143 (.in(nor_219_out), .en(IREO));  // open: out
  Driver driver_144 (.in(nor_221_out), .en(IREO));  // open: out
  Driver driver_145 (.in(nor_223_out), .en(IREO));  // open: out
  nor nor_225 (nor_225_out, and_407_out, nor_226_out);
  nor nor_226 (nor_226_out, nor_225_out, and_408_out);
  nor nor_227 (nor_227_out, and_409_out, nor_228_out);
  nor nor_228 (nor_228_out, nor_227_out, and_410_out);
  nor nor_229 (nor_229_out, and_411_out, nor_230_out);
  nor nor_230 (nor_230_out, nor_229_out, and_412_out);
  nor nor_231 (nor_231_out, and_413_out, nor_232_out);
  nor nor_232 (nor_232_out, nor_231_out, and_414_out);
  nor nor_233 (nor_233_out, and_415_out, nor_234_out);
  nor nor_234 (nor_234_out, nor_233_out, and_416_out);
  nor nor_235 (nor_235_out, and_417_out, nor_236_out);
  nor nor_236 (nor_236_out, nor_235_out, and_418_out);
  nor nor_237 (nor_237_out, and_419_out, nor_238_out);
  nor nor_238 (nor_238_out, nor_237_out, and_420_out);
  nor nor_239 (nor_239_out, and_421_out, nor_240_out);
  nor nor_240 (nor_240_out, nor_239_out, and_422_out);
  nor nor_241 (nor_241_out, and_423_out, nor_242_out);
  nor nor_242 (nor_242_out, nor_241_out, and_424_out);
  nor nor_243 (nor_243_out, and_425_out, nor_244_out);
  nor nor_244 (nor_244_out, nor_243_out, and_426_out);
  nor nor_245 (nor_245_out, and_427_out, nor_246_out);
  nor nor_246 (nor_246_out, nor_245_out, and_428_out);
  nor nor_247 (nor_247_out, and_429_out, nor_248_out);
  nor nor_248 (nor_248_out, nor_247_out, and_430_out);
  nor nor_249 (nor_249_out, and_431_out, nor_250_out);
  nor nor_250 (nor_250_out, nor_249_out, and_432_out);
  nor nor_251 (nor_251_out, and_433_out, nor_252_out);
  nor nor_252 (nor_252_out, nor_251_out, and_434_out);
  nor nor_253 (nor_253_out, and_435_out, nor_254_out);
  nor nor_254 (nor_254_out, nor_253_out, and_436_out);
  nor nor_255 (nor_255_out, and_437_out, nor_256_out);
  nor nor_256 (nor_256_out, nor_255_out, and_438_out);
  assign driver_146_out = and_99_out ? nor_225_out : 1'bz;  // Driver driver_146
  assign driver_146_out = and_101_out ? nor_227_out : 1'bz;  // Driver driver_147
  assign driver_146_out = and_103_out ? nor_229_out : 1'bz;  // Driver driver_148
  assign driver_146_out = and_105_out ? nor_231_out : 1'bz;  // Driver driver_149
  assign driver_146_out = and_107_out ? nor_233_out : 1'bz;  // Driver driver_150
  assign driver_146_out = and_109_out ? nor_235_out : 1'bz;  // Driver driver_151
  assign driver_146_out = and_111_out ? nor_237_out : 1'bz;  // Driver driver_152
  assign driver_146_out = and_113_out ? nor_239_out : 1'bz;  // Driver driver_153
  assign driver_146_out = and_115_out ? nor_241_out : 1'bz;  // Driver driver_154
  assign driver_146_out = and_117_out ? nor_243_out : 1'bz;  // Driver driver_155
  assign driver_146_out = and_119_out ? nor_245_out : 1'bz;  // Driver driver_156
  assign driver_146_out = and_121_out ? nor_247_out : 1'bz;  // Driver driver_157
  assign driver_146_out = and_123_out ? nor_249_out : 1'bz;  // Driver driver_158
  assign driver_146_out = and_125_out ? nor_251_out : 1'bz;  // Driver driver_159
  assign driver_146_out = and_127_out ? nor_253_out : 1'bz;  // Driver driver_160
  assign driver_146_out = and_129_out ? nor_255_out : 1'bz;  // Driver driver_161
  and and_439 (and_439_out, or_21_out, or_15_out);
  LED u_D0 (.in(nor_169_out));
  LED u_D1 (.in(nor_171_out));
  and and_440 (and_440_out, ~and_439_out, and_100_out);  // And
  and and_441 (and_441_out, and_100_out, and_439_out);
  and and_442 (and_442_out, ~and_439_out, and_102_out);  // And
  and and_443 (and_443_out, and_102_out, and_439_out);
  and and_444 (and_444_out, ~and_439_out, and_104_out);  // And
  and and_445 (and_445_out, and_104_out, and_439_out);
  and and_446 (and_446_out, ~and_439_out, and_106_out);  // And
  and and_447 (and_447_out, and_106_out, and_439_out);
  and and_448 (and_448_out, ~and_439_out, and_108_out);  // And
  and and_449 (and_449_out, and_108_out, and_439_out);
  and and_450 (and_450_out, ~and_439_out, and_110_out);  // And
  and and_451 (and_451_out, and_110_out, and_439_out);
  and and_452 (and_452_out, ~and_439_out, and_112_out);  // And
  and and_453 (and_453_out, and_112_out, and_439_out);
  and and_454 (and_454_out, ~and_439_out, and_114_out);  // And
  and and_455 (and_455_out, and_114_out, and_439_out);
  and and_456 (and_456_out, ~and_439_out, and_116_out);  // And
  and and_457 (and_457_out, and_116_out, and_439_out);
  and and_458 (and_458_out, ~and_439_out, and_118_out);  // And
  and and_459 (and_459_out, and_118_out, and_439_out);
  and and_460 (and_460_out, ~and_439_out, and_120_out);  // And
  and and_461 (and_461_out, and_120_out, and_439_out);
  and and_462 (and_462_out, ~and_439_out, and_122_out);  // And
  and and_463 (and_463_out, and_122_out, and_439_out);
  and and_464 (and_464_out, ~and_439_out, and_124_out);  // And
  and and_465 (and_465_out, and_124_out, and_439_out);
  and and_466 (and_466_out, ~and_439_out, and_126_out);  // And
  and and_467 (and_467_out, and_126_out, and_439_out);
  and and_468 (and_468_out, ~and_439_out, and_128_out);  // And
  and and_469 (and_469_out, and_128_out, and_439_out);
  and and_470 (and_470_out, ~and_439_out, and_130_out);  // And
  and and_471 (and_471_out, and_130_out, and_439_out);
  LED u_D2 (.in(nor_173_out));
  LED u_D3 (.in(nor_175_out));
  nor nor_257 (nor_257_out, and_440_out, nor_258_out);
  nor nor_258 (nor_258_out, nor_257_out, and_441_out);
  nor nor_259 (nor_259_out, and_442_out, nor_260_out);
  nor nor_260 (nor_260_out, nor_259_out, and_443_out);
  nor nor_261 (nor_261_out, and_444_out, nor_262_out);
  nor nor_262 (nor_262_out, nor_261_out, and_445_out);
  nor nor_263 (nor_263_out, and_446_out, nor_264_out);
  nor nor_264 (nor_264_out, nor_263_out, and_447_out);
  nor nor_265 (nor_265_out, and_448_out, nor_266_out);
  nor nor_266 (nor_266_out, nor_265_out, and_449_out);
  nor nor_267 (nor_267_out, and_450_out, nor_268_out);
  nor nor_268 (nor_268_out, nor_267_out, and_451_out);
  nor nor_269 (nor_269_out, and_452_out, nor_270_out);
  nor nor_270 (nor_270_out, nor_269_out, and_453_out);
  nor nor_271 (nor_271_out, and_454_out, nor_272_out);
  nor nor_272 (nor_272_out, nor_271_out, and_455_out);
  nor nor_273 (nor_273_out, and_456_out, nor_274_out);
  nor nor_274 (nor_274_out, nor_273_out, and_457_out);
  nor nor_275 (nor_275_out, and_458_out, nor_276_out);
  nor nor_276 (nor_276_out, nor_275_out, and_459_out);
  nor nor_277 (nor_277_out, and_460_out, nor_278_out);
  nor nor_278 (nor_278_out, nor_277_out, and_461_out);
  nor nor_279 (nor_279_out, and_462_out, nor_280_out);
  nor nor_280 (nor_280_out, nor_279_out, and_463_out);
  nor nor_281 (nor_281_out, and_464_out, nor_282_out);
  nor nor_282 (nor_282_out, nor_281_out, and_465_out);
  nor nor_283 (nor_283_out, and_466_out, nor_284_out);
  nor nor_284 (nor_284_out, nor_283_out, and_467_out);
  nor nor_285 (nor_285_out, and_468_out, nor_286_out);
  nor nor_286 (nor_286_out, nor_285_out, and_469_out);
  nor nor_287 (nor_287_out, and_470_out, nor_288_out);
  nor nor_288 (nor_288_out, nor_287_out, and_471_out);
  LED A0 (.in(nor_209_out));
  LED A1 (.in(nor_211_out));
  assign driver_162_out = and_99_out ? nor_257_out : 1'bz;  // Driver driver_162
  assign driver_162_out = and_101_out ? nor_259_out : 1'bz;  // Driver driver_163
  assign driver_162_out = and_103_out ? nor_261_out : 1'bz;  // Driver driver_164
  assign driver_162_out = and_105_out ? nor_263_out : 1'bz;  // Driver driver_165
  assign driver_162_out = and_107_out ? nor_265_out : 1'bz;  // Driver driver_166
  assign driver_162_out = and_109_out ? nor_267_out : 1'bz;  // Driver driver_167
  assign driver_162_out = and_111_out ? nor_269_out : 1'bz;  // Driver driver_168
  assign driver_162_out = and_113_out ? nor_271_out : 1'bz;  // Driver driver_169
  assign driver_162_out = and_115_out ? nor_273_out : 1'bz;  // Driver driver_170
  assign driver_162_out = and_117_out ? nor_275_out : 1'bz;  // Driver driver_171
  assign driver_162_out = and_119_out ? nor_277_out : 1'bz;  // Driver driver_172
  assign driver_162_out = and_121_out ? nor_279_out : 1'bz;  // Driver driver_173
  assign driver_162_out = and_123_out ? nor_281_out : 1'bz;  // Driver driver_174
  assign driver_162_out = and_125_out ? nor_283_out : 1'bz;  // Driver driver_175
  assign driver_162_out = and_127_out ? nor_285_out : 1'bz;  // Driver driver_176
  assign driver_162_out = and_129_out ? nor_287_out : 1'bz;  // Driver driver_177
  LED A2 (.in(nor_213_out));
  LED A3 (.in(nor_215_out));
  LED I0 (.in(nor_217_out));
  LED I1 (.in(nor_219_out));
  PullDown pulldown_1 (.out(driver_38_out));
  PullDown pulldown_2 (.out(driver_54_out));
  PullDown pulldown_3 (.out(driver_70_out));
  PullDown pulldown_4 (.out(driver_86_out));
  PullDown pulldown_5 (.out(driver_102_out));
  PullDown pulldown_6 (.out(driver_122_out));
  PullDown pulldown_7 (.out(driver_146_out));
  PullDown pulldown_8 (.out(driver_162_out));
  LED I2 (.in(nor_221_out));
  LED I3 (.in(nor_223_out));
  and and_472 (and_472_out, driver_27_out, MAN_CLK);
  and and_473 (and_473_out, CLK, ~driver_27_out);  // And
  or or_46 (or_46_out, and_473_out, and_472_out);
  LED D0_2 (.in(driver_38_out));
  LED D1_2 (.in(driver_54_out));
  LED D2_2 (.in(driver_70_out));
  LED D3_2 (.in(driver_86_out));
  LED u_D4 (.in(driver_102_out));
  and and_474 (and_474_out, EN, E0);
  LED u_D5 (.in(driver_122_out));
  LED u_D6 (.in(driver_146_out));
  and and_475 (and_475_out, EN, E1);
  LED u_D7 (.in(driver_162_out));
  assign driver_162_out = ALUEO ? xor_3_out : 1'bz;  // Driver driver_178
  assign driver_146_out = ALUEO ? xor_24_out : 1'bz;  // Driver driver_179
  assign driver_122_out = ALUEO ? xor_4_out : 1'bz;  // Driver driver_180
  assign driver_102_out = ALUEO ? xor_19_out : 1'bz;  // Driver driver_181
  assign driver_86_out = ALUEO ? xor_1_out : 1'bz;  // Driver driver_182
  assign driver_70_out = ALUEO ? xor_20_out : 1'bz;  // Driver driver_183
  assign driver_54_out = ALUEO ? xor_2_out : 1'bz;  // Driver driver_184
  assign driver_38_out = ALUEO ? xor_21_out : 1'bz;  // Driver driver_185
  and and_476 (and_476_out, EN, E2);
  Driver driver_186 (.in(D0), .en(and_474_out));  // open: out
  Driver driver_187 (.in(D1), .en(and_475_out));  // open: out
  LED S0 (.in(xor_21_out));
  and and_477 (and_477_out, EN, E3);
  Driver driver_188 (.in(D2), .en(and_476_out));  // open: out
  Driver driver_189 (.in(D3), .en(and_477_out));  // open: out
  LED S1 (.in(xor_2_out));
  LED S2 (.in(xor_20_out));
  and and_478 (and_478_out, EN, E4);
  Driver driver_190 (.in(D4), .en(and_478_out));  // open: out
  Driver driver_191 (.in(D5), .en(and_479_out));  // open: out
  LED S3 (.in(xor_1_out));
  LED S4 (.in(xor_19_out));
  and and_479 (and_479_out, EN, E5);
  Driver driver_192 (.in(D6), .en(and_480_out));  // open: out
  Driver driver_193 (.in(D7), .en(and_485_out));  // open: out
  not not_18 (not_18_out, or_46_out);
  not not_19 (not_19_out, not_18_out);
  LED S5 (.in(xor_4_out));
  LED S6 (.in(xor_24_out));
  not not_20 (not_20_out, or_46_out);
  not not_21 (not_21_out, not_20_out);
  assign driver_27_out = MAN_CLK___HLT ? MAN_CLK___HLT : 1'bz;  // Driver driver_194
  LED led_1 (.in(driver_27_out));
  PullDown pulldown_9 (.out(driver_27_out));
  and and_480 (and_480_out, EN, E6);
  and and_481 (and_481_out, PCDEF, ~PCEI);  // And
  and and_482 (and_482_out, or_46_out, ~not_19_out);  // And
  LED S7 (.in(xor_3_out));
  and and_483 (and_483_out, or_46_out, ~not_21_out);  // And
  not not_22 (not_22_out, or_46_out);
  not not_23 (not_23_out, not_22_out);
  and and_484 (and_484_out, or_46_out, ~not_23_out);  // And
  LED led_2 (.in(MEMLOAD));
  LED led_3 (.in(MEMEI));
  PullDown pulldown_10 (.out(MEMLOAD));
  PullDown pulldown_11 (.out(MEMEI));
  and and_485 (and_485_out, EN, E7);
  and and_486 (and_486_out, PCEI, driver_38_out);
  and and_487 (and_487_out, PCEI, driver_54_out);
  and and_488 (and_488_out, PCEI, driver_70_out);
  and and_489 (and_489_out, PCEI, driver_86_out);
  not not_24 (not_24_out, ALOAD);
  and and_490 (and_490_out, ALOAD, driver_38_out);
  or or_47 (or_47_out, and_514_out, and_490_out);
  and and_491 (and_491_out, ALOAD, driver_54_out);
  or or_48 (or_48_out, and_517_out, and_491_out);
  and and_492 (and_492_out, ALOAD, driver_70_out);
  or or_49 (or_49_out, and_520_out, and_492_out);
  and and_493 (and_493_out, ALOAD, driver_86_out);
  or or_50 (or_50_out, and_523_out, and_493_out);
  and and_494 (and_494_out, ALOAD, driver_102_out);
  or or_51 (or_51_out, and_526_out, and_494_out);
  and and_495 (and_495_out, ALOAD, driver_122_out);
  or or_52 (or_52_out, and_529_out, and_495_out);
  and and_496 (and_496_out, ALOAD, driver_146_out);
  or or_53 (or_53_out, and_532_out, and_496_out);
  and and_497 (and_497_out, ALOAD, driver_162_out);
  or or_54 (or_54_out, and_535_out, and_497_out);
  not not_25 (not_25_out, BLOAD);
  and and_498 (and_498_out, BLOAD, driver_38_out);
  or or_55 (or_55_out, and_538_out, and_498_out);
  and and_499 (and_499_out, BLOAD, driver_54_out);
  or or_56 (or_56_out, and_539_out, and_499_out);
  and and_500 (and_500_out, BLOAD, driver_70_out);
  or or_57 (or_57_out, and_540_out, and_500_out);
  and and_501 (and_501_out, BLOAD, driver_86_out);
  or or_58 (or_58_out, and_541_out, and_501_out);
  and and_502 (and_502_out, BLOAD, driver_102_out);
  or or_59 (or_59_out, and_542_out, and_502_out);
  and and_503 (and_503_out, BLOAD, driver_122_out);
  or or_60 (or_60_out, and_543_out, and_503_out);
  and and_504 (and_504_out, BLOAD, driver_146_out);
  or or_61 (or_61_out, and_544_out, and_504_out);
  and and_505 (and_505_out, BLOAD, driver_162_out);
  or or_62 (or_62_out, and_545_out, and_505_out);
  not not_26 (not_26_out, OLOAD);
  and and_506 (and_506_out, OLOAD, driver_38_out);
  and and_507 (and_507_out, OLOAD, driver_54_out);
  and and_508 (and_508_out, OLOAD, driver_70_out);
  and and_509 (and_509_out, OLOAD, driver_86_out);
  and and_510 (and_510_out, OLOAD, driver_102_out);
  and and_511 (and_511_out, OLOAD, driver_122_out);
  and and_512 (and_512_out, OLOAD, driver_146_out);
  and and_513 (and_513_out, OLOAD, driver_162_out);
  LED led_4 (.in(MEMEO));
  LED led_5 (.in(MARO));
  PullDown pulldown_12 (.out(MEMEO));
  PullDown pulldown_13 (.out(MARO));
  or or_63 (or_63_out, and_481_out, and_486_out);
  or or_64 (or_64_out, and_481_out, and_487_out);
  or or_65 (or_65_out, and_481_out, and_488_out);
  or or_66 (or_66_out, and_481_out, and_489_out);
  and and_514 (and_514_out, nor_289_out, not_24_out);
  and and_515 (and_515_out, ~or_47_out, and_482_out);  // And
  and and_516 (and_516_out, and_482_out, or_47_out);
  and and_517 (and_517_out, nor_291_out, not_24_out);
  and and_518 (and_518_out, ~or_48_out, and_482_out);  // And
  and and_519 (and_519_out, and_482_out, or_48_out);
  and and_520 (and_520_out, nor_293_out, not_24_out);
  and and_521 (and_521_out, ~or_49_out, and_482_out);  // And
  and and_522 (and_522_out, and_482_out, or_49_out);
  and and_523 (and_523_out, nor_295_out, not_24_out);
  and and_524 (and_524_out, ~or_50_out, and_482_out);  // And
  and and_525 (and_525_out, and_482_out, or_50_out);
  and and_526 (and_526_out, nor_297_out, not_24_out);
  and and_527 (and_527_out, ~or_51_out, and_482_out);  // And
  and and_528 (and_528_out, and_482_out, or_51_out);
  and and_529 (and_529_out, nor_299_out, not_24_out);
  and and_530 (and_530_out, ~or_52_out, and_482_out);  // And
  and and_531 (and_531_out, and_482_out, or_52_out);
  and and_532 (and_532_out, nor_301_out, not_24_out);
  and and_533 (and_533_out, ~or_53_out, and_482_out);  // And
  and and_534 (and_534_out, and_482_out, or_53_out);
  and and_535 (and_535_out, nor_303_out, not_24_out);
  and and_536 (and_536_out, ~or_54_out, and_482_out);  // And
  and and_537 (and_537_out, and_482_out, or_54_out);
  and and_538 (and_538_out, nor_305_out, not_25_out);
  and and_539 (and_539_out, nor_307_out, not_25_out);
  and and_540 (and_540_out, nor_309_out, not_25_out);
  and and_541 (and_541_out, nor_311_out, not_25_out);
  and and_542 (and_542_out, nor_313_out, not_25_out);
  and and_543 (and_543_out, nor_315_out, not_25_out);
  and and_544 (and_544_out, nor_317_out, not_25_out);
  and and_545 (and_545_out, nor_319_out, not_25_out);
  and and_546 (and_546_out, nor_321_out, not_26_out);
  or or_67 (or_67_out, and_546_out, and_506_out);
  and and_547 (and_547_out, nor_323_out, not_26_out);
  or or_68 (or_68_out, and_547_out, and_507_out);
  and and_548 (and_548_out, nor_325_out, not_26_out);
  or or_69 (or_69_out, and_548_out, and_508_out);
  and and_549 (and_549_out, nor_327_out, not_26_out);
  or or_70 (or_70_out, and_549_out, and_509_out);
  and and_550 (and_550_out, nor_329_out, not_26_out);
  or or_71 (or_71_out, and_550_out, and_510_out);
  and and_551 (and_551_out, nor_331_out, not_26_out);
  or or_72 (or_72_out, and_551_out, and_511_out);
  and and_552 (and_552_out, nor_333_out, not_26_out);
  or or_73 (or_73_out, and_552_out, and_512_out);
  and and_553 (and_553_out, nor_335_out, not_26_out);
  or or_74 (or_74_out, and_553_out, and_513_out);
  assign MARCLR = MASTER_RST ? MASTER_RST : 1'bz;  // Driver driver_195
  LED led_6 (.in(MARCLR));
  LED led_7 (.in(MARLOAD));
  PullDown pulldown_14 (.out(MARCLR));
  PullDown pulldown_15 (.out(MARLOAD));
  not not_27 (not_27_out, PCJ);
  or or_75 (or_75_out, and_594_out, and_597_out);
  or or_76 (or_76_out, and_586_out, and_598_out);
  or or_77 (or_77_out, and_587_out, and_595_out);
  and and_554 (and_554_out, ~or_55_out, and_483_out);  // And
  and and_555 (and_555_out, and_483_out, or_55_out);
  and and_556 (and_556_out, ~or_56_out, and_483_out);  // And
  and and_557 (and_557_out, and_483_out, or_56_out);
  and and_558 (and_558_out, ~or_57_out, and_483_out);  // And
  and and_559 (and_559_out, and_483_out, or_57_out);
  and and_560 (and_560_out, ~or_58_out, and_483_out);  // And
  and and_561 (and_561_out, and_483_out, or_58_out);
  and and_562 (and_562_out, ~or_59_out, and_483_out);  // And
  and and_563 (and_563_out, and_483_out, or_59_out);
  and and_564 (and_564_out, ~or_60_out, and_483_out);  // And
  and and_565 (and_565_out, and_483_out, or_60_out);
  and and_566 (and_566_out, ~or_61_out, and_483_out);  // And
  and and_567 (and_567_out, and_483_out, or_61_out);
  and and_568 (and_568_out, ~or_62_out, and_483_out);  // And
  and and_569 (and_569_out, and_483_out, or_62_out);
  and and_570 (and_570_out, ~or_67_out, and_484_out);  // And
  and and_571 (and_571_out, and_484_out, or_67_out);
  and and_572 (and_572_out, ~or_68_out, and_484_out);  // And
  and and_573 (and_573_out, and_484_out, or_68_out);
  and and_574 (and_574_out, ~or_69_out, and_484_out);  // And
  and and_575 (and_575_out, and_484_out, or_69_out);
  and and_576 (and_576_out, ~or_70_out, and_484_out);  // And
  and and_577 (and_577_out, and_484_out, or_70_out);
  and and_578 (and_578_out, ~or_71_out, and_484_out);  // And
  and and_579 (and_579_out, and_484_out, or_71_out);
  and and_580 (and_580_out, ~or_72_out, and_484_out);  // And
  and and_581 (and_581_out, and_484_out, or_72_out);
  and and_582 (and_582_out, ~or_73_out, and_484_out);  // And
  and and_583 (and_583_out, and_484_out, or_73_out);
  and and_584 (and_584_out, ~or_74_out, and_484_out);  // And
  and and_585 (and_585_out, and_484_out, or_74_out);
  LED led_8 (.in(IREO));
  LED led_9 (.in(IRCLR));
  PullDown pulldown_16 (.out(IREO));
  PullDown pulldown_17 (.out(IRCLR));
  not not_28 (not_28_out, or_46_out);
  not not_29 (not_29_out, not_28_out);
  not not_30 (not_30_out, PCJ);
  or or_78 (or_78_out, ACLR, and_515_out);
  nor nor_289 (nor_289_out, or_78_out, nor_290_out);
  nor nor_290 (nor_290_out, nor_289_out, and_516_out);
  or or_79 (or_79_out, ACLR, and_518_out);
  nor nor_291 (nor_291_out, or_79_out, nor_292_out);
  nor nor_292 (nor_292_out, nor_291_out, and_519_out);
  or or_80 (or_80_out, ACLR, and_521_out);
  nor nor_293 (nor_293_out, or_80_out, nor_294_out);
  nor nor_294 (nor_294_out, nor_293_out, and_522_out);
  or or_81 (or_81_out, ACLR, and_524_out);
  nor nor_295 (nor_295_out, or_81_out, nor_296_out);
  nor nor_296 (nor_296_out, nor_295_out, and_525_out);
  or or_82 (or_82_out, ACLR, and_527_out);
  nor nor_297 (nor_297_out, or_82_out, nor_298_out);
  nor nor_298 (nor_298_out, nor_297_out, and_528_out);
  or or_83 (or_83_out, ACLR, and_530_out);
  nor nor_299 (nor_299_out, or_83_out, nor_300_out);
  nor nor_300 (nor_300_out, nor_299_out, and_531_out);
  or or_84 (or_84_out, ACLR, and_533_out);
  nor nor_301 (nor_301_out, or_84_out, nor_302_out);
  nor nor_302 (nor_302_out, nor_301_out, and_534_out);
  or or_85 (or_85_out, ACLR, and_536_out);
  nor nor_303 (nor_303_out, or_85_out, nor_304_out);
  nor nor_304 (nor_304_out, nor_303_out, and_537_out);
  or or_86 (CO, and_593_out, and_596_out);
  and and_586 (and_586_out, xor_12_out, or_108_out);
  xor xor_1 (xor_1_out, xor_12_out, or_108_out);
  and and_587 (and_587_out, xor_5_out, or_109_out);
  xor xor_2 (xor_2_out, xor_5_out, or_109_out);
  or or_87 (or_87_out, BCLR, and_554_out);
  nor nor_305 (nor_305_out, or_87_out, nor_306_out);
  nor nor_306 (nor_306_out, nor_305_out, and_555_out);
  or or_88 (or_88_out, BCLR, and_556_out);
  nor nor_307 (nor_307_out, or_88_out, nor_308_out);
  nor nor_308 (nor_308_out, nor_307_out, and_557_out);
  or or_89 (or_89_out, BCLR, and_558_out);
  nor nor_309 (nor_309_out, or_89_out, nor_310_out);
  nor nor_310 (nor_310_out, nor_309_out, and_559_out);
  or or_90 (or_90_out, BCLR, and_560_out);
  nor nor_311 (nor_311_out, or_90_out, nor_312_out);
  nor nor_312 (nor_312_out, nor_311_out, and_561_out);
  or or_91 (or_91_out, BCLR, and_562_out);
  nor nor_313 (nor_313_out, or_91_out, nor_314_out);
  nor nor_314 (nor_314_out, nor_313_out, and_563_out);
  or or_92 (or_92_out, BCLR, and_564_out);
  nor nor_315 (nor_315_out, or_92_out, nor_316_out);
  nor nor_316 (nor_316_out, nor_315_out, and_565_out);
  or or_93 (or_93_out, BCLR, and_566_out);
  nor nor_317 (nor_317_out, or_93_out, nor_318_out);
  nor nor_318 (nor_318_out, nor_317_out, and_567_out);
  or or_94 (or_94_out, BCLR, and_568_out);
  nor nor_319 (nor_319_out, or_94_out, nor_320_out);
  nor nor_320 (nor_320_out, nor_319_out, and_569_out);
  or or_95 (or_95_out, OCLR, and_570_out);
  nor nor_321 (nor_321_out, or_95_out, nor_322_out);
  nor nor_322 (nor_322_out, nor_321_out, and_571_out);
  or or_96 (or_96_out, OCLR, and_572_out);
  nor nor_323 (nor_323_out, or_96_out, nor_324_out);
  nor nor_324 (nor_324_out, nor_323_out, and_573_out);
  or or_97 (or_97_out, OCLR, and_574_out);
  nor nor_325 (nor_325_out, or_97_out, nor_326_out);
  nor nor_326 (nor_326_out, nor_325_out, and_575_out);
  or or_98 (or_98_out, OCLR, and_576_out);
  nor nor_327 (nor_327_out, or_98_out, nor_328_out);
  nor nor_328 (nor_328_out, nor_327_out, and_577_out);
  or or_99 (or_99_out, OCLR, and_578_out);
  nor nor_329 (nor_329_out, or_99_out, nor_330_out);
  nor nor_330 (nor_330_out, nor_329_out, and_579_out);
  or or_100 (or_100_out, OCLR, and_580_out);
  nor nor_331 (nor_331_out, or_100_out, nor_332_out);
  nor nor_332 (nor_332_out, nor_331_out, and_581_out);
  or or_101 (or_101_out, OCLR, and_582_out);
  nor nor_333 (nor_333_out, or_101_out, nor_334_out);
  nor nor_334 (nor_334_out, nor_333_out, and_583_out);
  or or_102 (or_102_out, OCLR, and_584_out);
  nor nor_335 (nor_335_out, or_102_out, nor_336_out);
  nor nor_336 (nor_336_out, nor_335_out, and_585_out);
  assign IRCLR = MASTER_RST ? MASTER_RST : 1'bz;  // Driver driver_196
  LED led_10 (.in(IRLOAD));
  LED led_11 (.in(PCEI));
  PullDown pulldown_18 (.out(IRLOAD));
  PullDown pulldown_19 (.out(PCEI));
  and and_588 (and_588_out, or_46_out, ~not_29_out);  // And
  and and_589 (and_589_out, and_588_out, PCJ);
  and and_590 (and_590_out, nor_345_out, not_30_out);
  and and_591 (and_591_out, nor_347_out, not_30_out);
  and and_592 (and_592_out, nor_349_out, not_30_out);
  and and_593 (and_593_out, xor_10_out, or_106_out);
  xor xor_3 (xor_3_out, xor_10_out, or_106_out);
  and and_594 (and_594_out, xor_11_out, or_107_out);
  xor xor_4 (xor_4_out, xor_11_out, or_107_out);
  LED led_12 (.in(PCDEF));
  LED led_13 (.in(PCJ));
  PullDown pulldown_20 (.out(PCDEF));
  PullDown pulldown_21 (.out(PCJ));
  or or_103 (or_103_out, and_590_out, and_589_out);
  or or_104 (or_104_out, and_591_out, and_589_out);
  or or_105 (or_105_out, and_592_out, and_589_out);
  and and_595 (and_595_out, xor_17_out, xor_14_out);
  xor xor_5 (xor_5_out, xor_17_out, xor_14_out);
  assign PCJ = MASTER_RST ? MASTER_RST : 1'bz;  // Driver driver_197
  LED led_14 (.in(PCEO));
  LED led_15 (.in(ALOAD));
  PullDown pulldown_22 (.out(PCEO));
  PullDown pulldown_23 (.out(ALOAD));
  xor xor_6 (xor_6_out, or_63_out, ~not_27_out);  // XOr
  xor xor_7 (xor_7_out, or_64_out, ~not_27_out);  // XOr
  xor xor_8 (xor_8_out, or_65_out, ~not_27_out);  // XOr
  xor xor_9 (xor_9_out, or_66_out, ~not_27_out);  // XOr
  assign driver_38_out = AEO ? nor_289_out : 1'bz;  // Driver driver_198
  assign driver_54_out = AEO ? nor_291_out : 1'bz;  // Driver driver_199
  assign driver_70_out = AEO ? nor_293_out : 1'bz;  // Driver driver_200
  assign driver_86_out = AEO ? nor_295_out : 1'bz;  // Driver driver_201
  assign driver_102_out = AEO ? nor_297_out : 1'bz;  // Driver driver_202
  assign driver_122_out = AEO ? nor_299_out : 1'bz;  // Driver driver_203
  assign driver_146_out = AEO ? nor_301_out : 1'bz;  // Driver driver_204
  assign driver_162_out = AEO ? nor_303_out : 1'bz;  // Driver driver_205
  and and_596 (and_596_out, xor_36_out, xor_34_out);
  xor xor_10 (xor_10_out, xor_36_out, xor_34_out);
  and and_597 (and_597_out, xor_33_out, xor_26_out);
  xor xor_11 (xor_11_out, xor_33_out, xor_26_out);
  and and_598 (and_598_out, xor_25_out, xor_18_out);
  xor xor_12 (xor_12_out, xor_25_out, xor_18_out);
  assign driver_38_out = BEO ? nor_305_out : 1'bz;  // Driver driver_206
  assign driver_54_out = BEO ? nor_307_out : 1'bz;  // Driver driver_207
  assign driver_70_out = BEO ? nor_309_out : 1'bz;  // Driver driver_208
  assign driver_86_out = BEO ? nor_311_out : 1'bz;  // Driver driver_209
  assign driver_102_out = BEO ? nor_313_out : 1'bz;  // Driver driver_210
  assign driver_122_out = BEO ? nor_315_out : 1'bz;  // Driver driver_211
  assign driver_146_out = BEO ? nor_317_out : 1'bz;  // Driver driver_212
  assign driver_162_out = BEO ? nor_319_out : 1'bz;  // Driver driver_213
  assign driver_38_out = OEO ? nor_321_out : 1'bz;  // Driver driver_214
  assign driver_54_out = OEO ? nor_323_out : 1'bz;  // Driver driver_215
  assign driver_70_out = OEO ? nor_325_out : 1'bz;  // Driver driver_216
  assign driver_86_out = OEO ? nor_327_out : 1'bz;  // Driver driver_217
  assign driver_102_out = OEO ? nor_329_out : 1'bz;  // Driver driver_218
  assign driver_122_out = OEO ? nor_331_out : 1'bz;  // Driver driver_219
  assign driver_146_out = OEO ? nor_333_out : 1'bz;  // Driver driver_220
  assign driver_162_out = OEO ? nor_335_out : 1'bz;  // Driver driver_221
  assign ACLR = MASTER_RST ? MASTER_RST : 1'bz;  // Driver driver_222
  LED led_16 (.in(ACLR));
  LED led_17 (.in(AEO));
  PullDown pulldown_24 (.out(ACLR));
  PullDown pulldown_25 (.out(AEO));
  and and_599 (and_599_out, nor_346_out, or_63_out);
  and and_600 (and_600_out, xor_6_out, nor_345_out);
  and and_601 (and_601_out, nor_348_out, or_64_out);
  and and_602 (and_602_out, xor_7_out, nor_347_out);
  and and_603 (and_603_out, nor_350_out, or_65_out);
  and and_604 (and_604_out, xor_8_out, nor_349_out);
  and and_605 (and_605_out, nor_352_out, or_66_out);
  and and_606 (and_606_out, xor_9_out, nor_351_out);
  and and_607 (and_607_out, nor_289_out, ALUEAI);
  xor xor_13 (xor_13_out, and_607_out, ALUINVA);
  LED led_18 (.in(ALUINVA));
  LED led_19 (.in(ALUEAI));
  PullDown pulldown_26 (.out(ALUINVA));
  PullDown pulldown_27 (.out(ALUEAI));
  and and_608 (and_608_out, and_599_out, and_588_out);
  and and_609 (and_609_out, and_588_out, and_600_out);
  and and_610 (and_610_out, and_601_out, or_103_out);
  and and_611 (and_611_out, or_103_out, and_602_out);
  and and_612 (and_612_out, and_603_out, or_104_out);
  and and_613 (and_613_out, or_104_out, and_604_out);
  and and_614 (and_614_out, and_605_out, or_105_out);
  and and_615 (and_615_out, or_105_out, and_606_out);
  and and_616 (and_616_out, nor_291_out, ALUEAI);
  xor xor_14 (xor_14_out, and_616_out, ALUINVA);
  xor xor_15 (xor_15_out, ALUINVB, and_617_out);
  and and_617 (and_617_out, ALUEBI, nor_305_out);
  LED led_20 (.in(ALUCI));
  LED led_21 (.in(ALUEO));
  PullDown pulldown_28 (.out(ALUCI));
  PullDown pulldown_29 (.out(ALUEO));
  nor nor_337 (nor_337_out, and_608_out, nor_338_out);
  nor nor_338 (nor_338_out, nor_337_out, and_609_out);
  nor nor_339 (nor_339_out, and_610_out, nor_340_out);
  nor nor_340 (nor_340_out, nor_339_out, and_611_out);
  nor nor_341 (nor_341_out, and_612_out, nor_342_out);
  nor nor_342 (nor_342_out, nor_341_out, and_613_out);
  nor nor_343 (nor_343_out, and_614_out, nor_344_out);
  nor nor_344 (nor_344_out, nor_343_out, and_615_out);
  and and_618 (and_618_out, nor_293_out, ALUEAI);
  xor xor_16 (xor_16_out, and_618_out, ALUINVA);
  or or_106 (or_106_out, and_626_out, and_641_out);
  or or_107 (or_107_out, and_621_out, and_642_out);
  or or_108 (or_108_out, and_622_out, and_637_out);
  or or_109 (or_109_out, and_623_out, and_638_out);
  xor xor_17 (xor_17_out, ALUINVB, and_619_out);
  and and_619 (and_619_out, ALUEBI, nor_307_out);
  LED led_22 (.in(ALUEBI));
  LED led_23 (.in(ALUINVB));
  PullDown pulldown_30 (.out(ALUEBI));
  PullDown pulldown_31 (.out(ALUINVB));
  and and_620 (and_620_out, nor_295_out, ALUEAI);
  xor xor_18 (xor_18_out, and_620_out, ALUINVA);
  and and_621 (and_621_out, xor_32_out, or_76_out);
  xor xor_19 (xor_19_out, xor_32_out, or_76_out);
  and and_622 (and_622_out, xor_27_out, or_77_out);
  xor xor_20 (xor_20_out, xor_27_out, or_77_out);
  and and_623 (and_623_out, xor_28_out, ALUCI);
  xor xor_21 (xor_21_out, xor_28_out, ALUCI);
  xor xor_22 (xor_22_out, ALUINVB, and_624_out);
  and and_624 (and_624_out, ALUEBI, nor_309_out);
  LED led_24 (.in(BLOAD));
  LED led_25 (.in(BCLR));
  PullDown pulldown_32 (.out(BLOAD));
  PullDown pulldown_33 (.out(BCLR));
  not not_31 (not_31_out, and_588_out);
  not not_32 (not_32_out, or_103_out);
  not not_33 (not_33_out, or_104_out);
  not not_34 (not_34_out, or_105_out);
  LED D0_3 (.in(nor_289_out));
  LED D1_3 (.in(nor_291_out));
  and and_625 (and_625_out, nor_297_out, ALUEAI);
  xor xor_23 (xor_23_out, and_625_out, ALUINVA);
  and and_626 (and_626_out, xor_31_out, or_75_out);
  xor xor_24 (xor_24_out, xor_31_out, or_75_out);
  xor xor_25 (xor_25_out, ALUINVB, and_627_out);
  and and_627 (and_627_out, ALUEBI, nor_311_out);
  assign BCLR = MASTER_RST ? MASTER_RST : 1'bz;  // Driver driver_223
  LED led_26 (.in(BEO));
  LED led_27 (.in(OLOAD));
  PullDown pulldown_34 (.out(BEO));
  PullDown pulldown_35 (.out(OLOAD));
  and and_628 (and_628_out, nor_337_out, not_31_out);
  and and_629 (and_629_out, not_31_out, nor_338_out);
  and and_630 (and_630_out, nor_339_out, not_32_out);
  and and_631 (and_631_out, not_32_out, nor_340_out);
  and and_632 (and_632_out, nor_341_out, not_33_out);
  and and_633 (and_633_out, not_33_out, nor_342_out);
  and and_634 (and_634_out, nor_343_out, not_34_out);
  and and_635 (and_635_out, not_34_out, nor_344_out);
  LED D2_3 (.in(nor_293_out));
  LED D3_3 (.in(nor_295_out));
  and and_636 (and_636_out, nor_299_out, ALUEAI);
  xor xor_26 (xor_26_out, and_636_out, ALUINVA);
  and and_637 (and_637_out, xor_22_out, xor_16_out);
  xor xor_27 (xor_27_out, xor_22_out, xor_16_out);
  and and_638 (and_638_out, xor_15_out, xor_13_out);
  xor xor_28 (xor_28_out, xor_15_out, xor_13_out);
  xor xor_29 (xor_29_out, ALUINVB, and_639_out);
  and and_639 (and_639_out, ALUEBI, nor_313_out);
  assign OCLR = MASTER_RST ? MASTER_RST : 1'bz;  // Driver driver_224
  LED led_28 (.in(OCLR));
  LED led_29 (.in(OEO));
  PullDown pulldown_36 (.out(OCLR));
  PullDown pulldown_37 (.out(OEO));
  nor nor_345 (nor_345_out, and_628_out, nor_346_out);
  nor nor_346 (nor_346_out, nor_345_out, and_629_out);
  nor nor_347 (nor_347_out, and_630_out, nor_348_out);
  nor nor_348 (nor_348_out, nor_347_out, and_631_out);
  nor nor_349 (nor_349_out, and_632_out, nor_350_out);
  nor nor_350 (nor_350_out, nor_349_out, and_633_out);
  nor nor_351 (nor_351_out, and_634_out, nor_352_out);
  nor nor_352 (nor_352_out, nor_351_out, and_635_out);
  LED D4_2 (.in(nor_297_out));
  LED D5_2 (.in(nor_299_out));
  and and_640 (and_640_out, nor_301_out, ALUEAI);
  xor xor_30 (xor_30_out, and_640_out, ALUINVA);
  and and_641 (and_641_out, xor_35_out, xor_30_out);
  xor xor_31 (xor_31_out, xor_35_out, xor_30_out);
  and and_642 (and_642_out, xor_29_out, xor_23_out);
  xor xor_32 (xor_32_out, xor_29_out, xor_23_out);
  xor xor_33 (xor_33_out, ALUINVB, and_643_out);
  and and_643 (and_643_out, ALUEBI, nor_315_out);
  LED D6_2 (.in(nor_301_out));
  LED D7_2 (.in(nor_303_out));
  and and_644 (and_644_out, nor_303_out, ALUEAI);
  xor xor_34 (xor_34_out, and_644_out, ALUINVA);
  xor xor_35 (xor_35_out, ALUINVB, and_645_out);
  and and_645 (and_645_out, ALUEBI, nor_317_out);
  LED D0_4 (.in(nor_305_out));
  xor xor_36 (xor_36_out, ALUINVB, and_646_out);
  and and_646 (and_646_out, ALUEBI, nor_319_out);
  LED D1_4 (.in(nor_307_out));
  LED D2_4 (.in(nor_309_out));
  LED D3_4 (.in(nor_311_out));
  LED D4_3 (.in(nor_313_out));
  assign driver_38_out = PCEO ? nor_345_out : 1'bz;  // Driver driver_225
  assign driver_54_out = PCEO ? nor_347_out : 1'bz;  // Driver driver_226
  assign driver_70_out = PCEO ? nor_349_out : 1'bz;  // Driver driver_227
  assign driver_86_out = PCEO ? nor_351_out : 1'bz;  // Driver driver_228
  LED D5_3 (.in(nor_315_out));
  LED D6_3 (.in(nor_317_out));
  LED D7_3 (.in(nor_319_out));
  not not_35 (not_35_out, nor_329_out);
  LED D0_5 (.in(nor_345_out));
  LED D1_5 (.in(nor_347_out));
  not not_36 (not_36_out, nor_331_out);
  LED D3_5 (.in(nor_349_out));
  LED D3_6 (.in(nor_351_out));
  not not_37 (not_37_out, nor_333_out);
  not not_38 (not_38_out, nor_335_out);
  and and_647 (and_647_out, not_38_out, not_37_out);
  and and_648 (and_648_out, not_36_out, nor_329_out);
  and and_649 (and_649_out, not_38_out, nor_333_out);
  and and_650 (and_650_out, not_36_out, not_35_out);
  and and_651 (and_651_out, nor_331_out, nor_329_out);
  and and_652 (and_652_out, nor_335_out, not_37_out);
  and and_653 (and_653_out, nor_331_out, not_35_out);
  and and_654 (and_654_out, nor_335_out, nor_333_out);
  and and_655 (and_655_out, and_647_out, and_648_out);
  and and_656 (and_656_out, and_649_out, and_650_out);
  and and_657 (and_657_out, and_649_out, and_651_out);
  and and_658 (and_658_out, and_652_out, and_653_out);
  and and_659 (and_659_out, and_654_out, and_651_out);
  and and_660 (and_660_out, and_653_out, and_647_out);
  and and_661 (and_661_out, and_654_out, and_650_out);
  and and_662 (and_662_out, and_654_out, and_653_out);
  and and_663 (and_663_out, and_649_out, and_648_out);
  and and_664 (and_664_out, and_649_out, and_653_out);
  and and_665 (and_665_out, and_652_out, and_651_out);
  and and_666 (and_666_out, and_654_out, and_648_out);
  and and_667 (and_667_out, and_647_out, and_651_out);
  and and_668 (and_668_out, and_652_out, and_648_out);
  assign driver_229_out = and_655_out ? and_655_out : 1'bz;  // Driver driver_229
  assign driver_229_out = and_656_out ? and_656_out : 1'bz;  // Driver driver_230
  assign driver_229_out = and_657_out ? and_657_out : 1'bz;  // Driver driver_231
  assign driver_229_out = and_658_out ? and_658_out : 1'bz;  // Driver driver_232
  assign driver_229_out = and_659_out ? and_659_out : 1'bz;  // Driver driver_233
  assign driver_234_out = and_660_out ? and_660_out : 1'bz;  // Driver driver_234
  assign driver_234_out = and_661_out ? and_661_out : 1'bz;  // Driver driver_235
  assign driver_234_out = and_662_out ? and_662_out : 1'bz;  // Driver driver_236
  assign driver_237_out = and_663_out ? and_663_out : 1'bz;  // Driver driver_237
  assign driver_237_out = and_664_out ? and_664_out : 1'bz;  // Driver driver_238
  assign driver_237_out = and_665_out ? and_665_out : 1'bz;  // Driver driver_239
  assign driver_240_out = and_666_out ? and_666_out : 1'bz;  // Driver driver_240
  assign driver_241_out = and_667_out ? and_667_out : 1'bz;  // Driver driver_241
  assign driver_241_out = and_668_out ? and_668_out : 1'bz;  // Driver driver_242
  assign driver_234_out = and_659_out ? and_659_out : 1'bz;  // Driver driver_243
  assign driver_237_out = and_661_out ? and_661_out : 1'bz;  // Driver driver_244
  assign driver_237_out = and_659_out ? and_659_out : 1'bz;  // Driver driver_245
  assign driver_237_out = and_662_out ? and_662_out : 1'bz;  // Driver driver_246
  and and_669 (and_669_out, and_647_out, and_650_out);
  PullDown pulldown_38 (.out(driver_240_out));
  assign driver_240_out = and_655_out ? and_655_out : 1'bz;  // Driver driver_247
  assign driver_240_out = and_656_out ? and_656_out : 1'bz;  // Driver driver_248
  assign driver_240_out = and_665_out ? and_665_out : 1'bz;  // Driver driver_249
  assign driver_241_out = and_655_out ? and_655_out : 1'bz;  // Driver driver_250
  assign driver_241_out = and_656_out ? and_656_out : 1'bz;  // Driver driver_251
  assign driver_241_out = and_663_out ? and_663_out : 1'bz;  // Driver driver_252
  assign driver_241_out = and_657_out ? and_657_out : 1'bz;  // Driver driver_253
  assign driver_254_out = and_655_out ? and_655_out : 1'bz;  // Driver driver_254
  assign driver_254_out = and_660_out ? and_660_out : 1'bz;  // Driver driver_255
  assign driver_254_out = and_667_out ? and_667_out : 1'bz;  // Driver driver_256
  assign driver_254_out = and_657_out ? and_657_out : 1'bz;  // Driver driver_257
  assign driver_254_out = and_666_out ? and_666_out : 1'bz;  // Driver driver_258
  assign driver_259_out = and_655_out ? and_655_out : 1'bz;  // Driver driver_259
  assign driver_259_out = and_657_out ? and_657_out : 1'bz;  // Driver driver_260
  assign driver_259_out = and_661_out ? and_661_out : 1'bz;  // Driver driver_261
  assign driver_259_out = and_669_out ? and_669_out : 1'bz;  // Driver driver_262
  PullDown pulldown_39 (.out(driver_229_out));
  PullDown pulldown_40 (.out(driver_234_out));
  PullDown pulldown_41 (.out(driver_237_out));
  not not_39 (not_39_out, driver_229_out);
  not not_40 (not_40_out, driver_234_out);
  not not_41 (not_41_out, driver_237_out);
  not not_42 (not_42_out, driver_240_out);
  not not_43 (not_43_out, driver_241_out);
  not not_44 (not_44_out, driver_254_out);
  not not_45 (not_45_out, driver_259_out);
  PullDown pulldown_42 (.out(driver_241_out));
  PullDown pulldown_43 (.out(driver_254_out));
  PullDown pulldown_44 (.out(driver_259_out));
  Seven_Seg seven_seg_1 (
    .a(not_42_out), .b(not_41_out), .c(not_40_out), .d(not_39_out), .e(not_43_out), .f(not_44_out),
    .g(not_45_out), .dp(1'b0));
  Seven_Seg seven_seg_2 (
    .a(not_53_out), .b(not_52_out), .c(not_51_out), .d(not_50_out), .e(not_54_out), .f(not_55_out),
    .g(not_56_out), .dp(1'b0));
  not not_46 (not_46_out, nor_321_out);
  not not_47 (not_47_out, nor_323_out);
  not not_48 (not_48_out, nor_325_out);
  not not_49 (not_49_out, nor_327_out);
  and and_670 (and_670_out, not_49_out, not_48_out);
  and and_671 (and_671_out, not_47_out, nor_321_out);
  and and_672 (and_672_out, not_49_out, nor_325_out);
  and and_673 (and_673_out, not_47_out, not_46_out);
  and and_674 (and_674_out, nor_323_out, nor_321_out);
  and and_675 (and_675_out, nor_327_out, not_48_out);
  and and_676 (and_676_out, nor_323_out, not_46_out);
  and and_677 (and_677_out, nor_327_out, nor_325_out);
  and and_678 (and_678_out, and_670_out, and_671_out);
  and and_679 (and_679_out, and_672_out, and_673_out);
  and and_680 (and_680_out, and_672_out, and_674_out);
  and and_681 (and_681_out, and_675_out, and_676_out);
  and and_682 (and_682_out, and_677_out, and_674_out);
  and and_683 (and_683_out, and_676_out, and_670_out);
  and and_684 (and_684_out, and_677_out, and_673_out);
  and and_685 (and_685_out, and_677_out, and_676_out);
  and and_686 (and_686_out, and_672_out, and_671_out);
  and and_687 (and_687_out, and_672_out, and_676_out);
  and and_688 (and_688_out, and_675_out, and_674_out);
  and and_689 (and_689_out, and_677_out, and_671_out);
  and and_690 (and_690_out, and_670_out, and_674_out);
  and and_691 (and_691_out, and_675_out, and_671_out);
  assign driver_263_out = and_678_out ? and_678_out : 1'bz;  // Driver driver_263
  assign driver_263_out = and_679_out ? and_679_out : 1'bz;  // Driver driver_264
  assign driver_263_out = and_680_out ? and_680_out : 1'bz;  // Driver driver_265
  assign driver_263_out = and_681_out ? and_681_out : 1'bz;  // Driver driver_266
  assign driver_263_out = and_682_out ? and_682_out : 1'bz;  // Driver driver_267
  assign driver_268_out = and_683_out ? and_683_out : 1'bz;  // Driver driver_268
  assign driver_268_out = and_684_out ? and_684_out : 1'bz;  // Driver driver_269
  assign driver_268_out = and_685_out ? and_685_out : 1'bz;  // Driver driver_270
  assign driver_271_out = and_686_out ? and_686_out : 1'bz;  // Driver driver_271
  assign driver_271_out = and_687_out ? and_687_out : 1'bz;  // Driver driver_272
  assign driver_271_out = and_688_out ? and_688_out : 1'bz;  // Driver driver_273
  assign driver_274_out = and_689_out ? and_689_out : 1'bz;  // Driver driver_274
  assign driver_275_out = and_690_out ? and_690_out : 1'bz;  // Driver driver_275
  assign driver_275_out = and_691_out ? and_691_out : 1'bz;  // Driver driver_276
  assign driver_268_out = and_682_out ? and_682_out : 1'bz;  // Driver driver_277
  and and_692 (and_692_out, and_670_out, and_673_out);
  assign driver_271_out = and_684_out ? and_684_out : 1'bz;  // Driver driver_278
  assign driver_271_out = and_682_out ? and_682_out : 1'bz;  // Driver driver_279
  assign driver_271_out = and_685_out ? and_685_out : 1'bz;  // Driver driver_280
  assign driver_274_out = and_678_out ? and_678_out : 1'bz;  // Driver driver_281
  assign driver_274_out = and_679_out ? and_679_out : 1'bz;  // Driver driver_282
  assign driver_274_out = and_688_out ? and_688_out : 1'bz;  // Driver driver_283
  assign driver_275_out = and_678_out ? and_678_out : 1'bz;  // Driver driver_284
  assign driver_275_out = and_679_out ? and_679_out : 1'bz;  // Driver driver_285
  assign driver_275_out = and_686_out ? and_686_out : 1'bz;  // Driver driver_286
  assign driver_275_out = and_680_out ? and_680_out : 1'bz;  // Driver driver_287
  assign driver_288_out = and_678_out ? and_678_out : 1'bz;  // Driver driver_288
  assign driver_288_out = and_683_out ? and_683_out : 1'bz;  // Driver driver_289
  assign driver_288_out = and_690_out ? and_690_out : 1'bz;  // Driver driver_290
  assign driver_288_out = and_680_out ? and_680_out : 1'bz;  // Driver driver_291
  assign driver_288_out = and_689_out ? and_689_out : 1'bz;  // Driver driver_292
  assign driver_293_out = and_678_out ? and_678_out : 1'bz;  // Driver driver_293
  assign driver_293_out = and_680_out ? and_680_out : 1'bz;  // Driver driver_294
  assign driver_293_out = and_684_out ? and_684_out : 1'bz;  // Driver driver_295
  PullDown pulldown_45 (.out(driver_263_out));
  PullDown pulldown_46 (.out(driver_268_out));
  PullDown pulldown_47 (.out(driver_271_out));
  PullDown pulldown_48 (.out(driver_274_out));
  assign driver_293_out = and_692_out ? and_692_out : 1'bz;  // Driver driver_296
  not not_50 (not_50_out, driver_263_out);
  not not_51 (not_51_out, driver_268_out);
  not not_52 (not_52_out, driver_271_out);
  not not_53 (not_53_out, driver_274_out);
  not not_54 (not_54_out, driver_275_out);
  not not_55 (not_55_out, driver_288_out);
  not not_56 (not_56_out, driver_293_out);
  PullDown pulldown_49 (.out(driver_275_out));
  PullDown pulldown_50 (.out(driver_288_out));
  PullDown pulldown_51 (.out(driver_293_out));

  // Notes on the sheet:
  //   CLK: Hz: 50
  //   E0: default 1
  //   E1: default 1
  //   E2: default 1
  //   E3: default 1
  //   E4: default 1
  //   E5: default 1
  //   E6: default 1
  //   E7: default 1
  //   MAN_CLK___HLT: default 1
  //   MASTER_RST: default 1
  //   Order for
  //   instructions:
  //   immediate then instruction
  //   Ex: 1111 0001 = LDA 15
  //   LDA ( 0001 )
  //   LDB ( 0010 )
  //   OUT ( 1110 )
  //   HLT ( 1111 )
  //   SUM ( 0011 )
  //   SUB ( 0100 )
  //   STA ( 0101 )
  //   STB ( 0110 )
  //   LDAI ( 0111 )
  //   LDBI ( 1000 )
  //   JMP ( 1001 )
  //   Bus
  //   Memory Address Register (MAR)
  //   Instruction Register
  //   ALU
  //   The double not gates fix
  //   a racing issue between
  //   CLKMOD and INPUTMOD
  //   INPUTMOD
  //   ~CLKMOD
  //   Register A
  //   Register B
  //   Program Counter (PC)
  //   Output Register
endmodule
